// Logisim project 4bit counter.circ as structural Verilog: 8 circuits, main circuit bit counter
module bit_counter (
  input  in_1,
  input  in_2,
  input  [3:0] in_3,
  input  in_4,
  input  in_5,
  output [3:0] out_6
);

  wire and_1_out, and_2_out, and_3_out, and_4_out, and_5_out, and_6_out, and_7_out, and_8_out, and_9_out,
       and_10_out, and_11_out, not_1_out, not_2_out, not_3_out, not_4_out, or_1_out, or_2_out, or_3_out,
       or_4_out, or_5_out, or_6_out, or_7_out, or_8_out;

  not not_1 (not_1_out, in_3[3]);
  not not_2 (not_2_out, in_3[2]);
  not not_3 (not_3_out, in_3[1]);
  and and_1 (and_1_out, in_1, not_1_out);
  and and_2 (and_2_out, in_1, not_2_out);
  and and_3 (and_3_out, not_3_out, in_1);
  not not_4 (not_4_out, in_3[0]);
  and and_4 (and_4_out, in_1, in_3[3]);
  and and_5 (and_5_out, in_3[2], in_1);
  and and_6 (and_6_out, in_5, and_7_out, out_6[1]);
  and and_7 (and_7_out, in_5, out_6[0]);
  and and_8 (and_8_out, in_3[0], in_1);
  and and_9 (and_9_out, not_4_out, in_1);
  or or_1 (or_1_out, and_1_out, and_10_out);
  and and_10 (and_10_out, in_5, and_6_out, out_6[2]);
  or or_2 (or_2_out, and_2_out, and_6_out);
  and and_11 (and_11_out, in_1, in_3[1]);
  or or_3 (or_3_out, and_3_out, and_7_out);
  or or_4 (or_4_out, and_8_out, in_5);
  or or_5 (or_5_out, in_5, and_9_out);
  or or_6 (or_6_out, and_4_out, and_10_out);
  or or_7 (or_7_out, and_5_out, and_6_out);
  or or_8 (or_8_out, and_11_out, and_7_out);
  J_K_Flip_Flop j_k_ff_1 (.J(or_6_out), .clk(in_4), .K(or_1_out), .Q(out_6[3]), .reset(in_2));  // open: Qn, preset, en
  J_K_Flip_Flop j_k_ff_2 (.J(or_7_out), .clk(in_4), .K(or_2_out), .Q(out_6[2]), .reset(in_2));  // open: Qn, preset, en
  J_K_Flip_Flop j_k_ff_3 (.J(or_8_out), .clk(in_4), .K(or_3_out), .Q(out_6[1]), .reset(in_2));  // open: Qn, preset, en
  J_K_Flip_Flop j_k_ff_4 (.J(or_4_out), .clk(in_4), .K(or_5_out), .Q(out_6[0]), .reset(in_2));  // open: Qn, preset, en
endmodule

module number_display (
  input  in_1,
  input  in_2,
  input  in_3,
  input  in_4,
  input  in_5,
  input  in_6,
  input  in_7,
  input  in_8,
  input  in_9,
  output [3:0] out_10,
  output [3:0] out_11
);

  wire bit_counter_1_p5, bit_counter_1_p6, bit_counter_1_p7, bit_counter_1_p8, bit_counter_1_p9,
       bit_counter_1_p10, bit_counter_2_p7, bit_counter_2_p8, bit_counter_2_p9, bit_counter_2_p10,
       clock_1_out, or_1_out;
  wire [7:0] bcd_decoder_num_1_p5, bcd_decoder_num_2_p5;

  // bit_counter bit_counter_1: pin names not known; wires that end beside it: in_3, in_5, in_7, in_8, bit_counter_1_p5, bit_counter_1_p6, bit_counter_1_p7, bit_counter_1_p8, bit_counter_1_p9, bit_counter_1_p10
  // BCD_DECODER_num bcd_decoder_num_1: pin names not known; wires that end beside it: bit_counter_1_p7, bit_counter_1_p8, bit_counter_1_p9, bit_counter_1_p10, bcd_decoder_num_1_p5, out_11
  or or_1 (or_1_out, in_4, bit_counter_1_p6);
  Clock clock_1 (.out(clock_1_out));
  _7_Segment_Display u_7_segment_display_1 (
    .g(bcd_decoder_num_2_p5[7]), .f(bcd_decoder_num_2_p5[6]), .a(bcd_decoder_num_2_p5[5]),
    .b(bcd_decoder_num_2_p5[4]), .e(bcd_decoder_num_2_p5[3]), .d(bcd_decoder_num_2_p5[2]),
    .c(bcd_decoder_num_2_p5[1]), .dp(bcd_decoder_num_2_p5[0]));
  _7_Segment_Display u_7_segment_display_2 (
    .g(bcd_decoder_num_1_p5[7]), .f(bcd_decoder_num_1_p5[6]), .a(bcd_decoder_num_1_p5[5]),
    .b(bcd_decoder_num_1_p5[4]), .e(bcd_decoder_num_1_p5[3]), .d(bcd_decoder_num_1_p5[2]),
    .c(bcd_decoder_num_1_p5[1]), .dp(bcd_decoder_num_1_p5[0]));
  // bit_counter bit_counter_2: pin names not known; wires that end beside it: in_1, in_2, or_1_out, in_6, clock_1_out, in_9, bit_counter_2_p7, bit_counter_2_p8, bit_counter_2_p9, bit_counter_2_p10, bit_counter_1_p5
  // BCD_DECODER_num bcd_decoder_num_2: pin names not known; wires that end beside it: bit_counter_2_p7, bit_counter_2_p8, bit_counter_2_p9, bit_counter_2_p10, bcd_decoder_num_2_p5, bit_counter_1_p6, out_10
endmodule

module display (
  input  in_1,
  input  in_2,
  input  in_3,
  input  in_4,
  input  in_5,
  input  in_6,
  input  in_7,
  input  in_8,
  input  in_9,
  output out_10,
  output [3:0] out_11,
  output [3:0] out_12
);

  wire and_1_out, and_2_out, and_3_out, and_4_out, and_5_out, and_6_out, and_7_out, and_8_out, and_9_out,
       and_10_out, and_11_out, and_12_out, and_13_out, and_14_out, and_15_out, and_16_out, and_17_out,
       bit_counter_1_p11, clock_1_out, not_1_out, not_2_out, not_3_out, not_4_out, not_5_out, or_1_out,
       or_2_out, or_3_out, or_4_out, or_5_out, or_6_out, or_7_out, or_8_out;

  Clock clock_1 (.out(clock_1_out));
  or or_1 (or_1_out, in_3, and_17_out);
  // bit_counter bit_counter_1: pin names not known; wires that end beside it: in_1, in_2, or_1_out, in_4, clock_1_out, in_5, out_12[0], out_12[1], out_12[2], out_12[3], bit_counter_1_p11, out_10
  not not_1 (not_1_out, out_12[0]);
  not not_2 (not_2_out, out_12[1]);
  not not_3 (not_3_out, out_12[2]);
  not not_4 (not_4_out, out_12[3]);
  and and_1 (and_1_out, not_1_out, not_3_out);
  or or_2 (or_2_out, and_1_out, out_12[1], out_12[3], and_2_out);
  and and_2 (and_2_out, out_12[0], out_12[2]);
  and and_3 (and_3_out, not_1_out, not_2_out);
  or or_3 (or_3_out, and_3_out, not_3_out, and_4_out);
  and and_4 (and_4_out, out_12[0], out_12[1]);
  and and_5 (and_5_out, not_1_out, not_2_out);
  or or_4 (or_4_out, and_5_out, and_6_out, and_7_out, out_12[3]);
  and and_6 (and_6_out, out_12[2], not_1_out);
  and and_7 (and_7_out, not_2_out, out_12[2]);
  and and_8 (and_8_out, out_12[2], not_2_out);
  or or_5 (or_5_out, and_8_out, and_9_out, and_10_out, out_12[3]);
  and and_9 (and_9_out, out_12[1], not_3_out);
  and and_10 (and_10_out, out_12[2], not_1_out);
  and and_11 (and_11_out, not_1_out, out_12[1]);
  or or_6 (or_6_out, and_11_out, and_12_out);
  and and_12 (and_12_out, not_1_out, not_3_out);
  and and_13 (and_13_out, out_12[0], not_2_out, out_12[2]);
  and and_14 (and_14_out, out_12[1], not_1_out);
  or or_7 (or_7_out, and_13_out, and_14_out, and_15_out, and_16_out, out_12[3]);
  and and_15 (and_15_out, not_3_out, out_12[1]);
  and and_16 (and_16_out, not_3_out, not_1_out);
  or or_8 (or_8_out, not_2_out, out_12[0], out_12[2]);
  not not_5 (not_5_out, or_8_out);
  _7_Segment_Display u_7_segment_display_1 (
    .g(or_5_out), .f(or_4_out), .a(or_2_out), .b(or_3_out), .e(or_6_out), .d(or_7_out), .c(or_8_out));  // open: dp
  and and_17 (and_17_out, not_5_out, or_5_out, or_4_out, or_3_out, or_2_out, or_7_out, or_6_out);
  // bit_counter bit_counter_2: pin names not known; wires that end beside it: in_6, in_7, in_8, in_9, bit_counter_1_p11, and_17_out, out_11[0], out_11[1], out_11[2], out_11[3]
endmodule

module BCD_DECODER_num (
  input  in_1,
  input  in_2,
  input  in_3,
  input  in_4,
  output [7:0] out_5,
  output out_6,
  output [3:0] out_7
);

  wire and_1_out, and_2_out, and_3_out, and_4_out, and_5_out, and_6_out, and_7_out, and_8_out, and_9_out,
       and_10_out, and_11_out, and_12_out, and_13_out, and_14_out, and_15_out, and_16_out, not_1_out,
       not_2_out, not_3_out, not_4_out, not_5_out;

  not not_1 (not_1_out, in_1);
  not not_2 (not_2_out, in_2);
  not not_3 (not_3_out, in_3);
  not not_4 (not_4_out, in_4);
  and and_1 (and_1_out, not_1_out, not_3_out);
  or or_1 (out_5[5], and_1_out, in_2, in_4, and_2_out);
  and and_2 (and_2_out, in_1, in_3);
  and and_3 (and_3_out, not_1_out, not_2_out);
  or or_2 (out_5[4], and_3_out, not_3_out, and_4_out);
  and and_4 (and_4_out, in_1, in_2);
  and and_5 (and_5_out, not_1_out, not_2_out);
  or or_3 (out_5[6], and_5_out, and_6_out, and_7_out, in_4);
  and and_6 (and_6_out, in_3, not_1_out);
  and and_7 (and_7_out, not_2_out, in_3);
  and and_8 (and_8_out, in_3, not_2_out);
  or or_4 (out_5[7], and_8_out, and_9_out, and_10_out, in_4);
  and and_9 (and_9_out, in_2, not_3_out);
  and and_10 (and_10_out, in_3, not_1_out);
  and and_11 (and_11_out, not_1_out, in_2);
  or or_5 (out_5[3], and_11_out, and_12_out);
  and and_12 (and_12_out, not_1_out, not_3_out);
  and and_13 (and_13_out, in_1, not_2_out, in_3);
  and and_14 (and_14_out, in_2, not_1_out);
  or or_6 (out_5[2], and_13_out, and_14_out, and_15_out, and_16_out, in_4);
  and and_15 (and_15_out, not_3_out, in_2);
  and and_16 (and_16_out, not_3_out, not_1_out);
  or or_7 (out_5[1], not_2_out, in_1, in_3);
  not not_5 (not_5_out, out_5[1]);
  _7_Segment_Display u_7_segment_display_1 (
    .g(out_5[7]), .f(out_5[6]), .a(out_5[5]), .b(out_5[4]), .e(out_5[3]), .d(out_5[2]), .c(out_5[1]));  // open: dp
  and and_17 (out_6, not_5_out, out_5[7], out_5[6], out_5[4], out_5[5], out_5[2], out_5[3]);

  assign out_7 = {in_4, in_3, in_2, in_1};
endmodule

module clock (
);

  wire clock_1_out, controlled_buffer_1_out, undriven;
  wire [6:0] undriven_2;

  Clock clock_1 (.out(clock_1_out));
  Keyboard keyboard_1 ();  // open: clk, re, clr, avail, data
  assign controlled_buffer_1_out = undriven ? clock_1_out : 1'bz;  // Controlled_Buffer controlled_buffer_1
  TTY tty_1 (.data(undriven_2), .clk(clock_1_out));  // open: we, clr
endmodule

module BCD_Decoder (
  input  in_1,
  input  in_2,
  input  in_3,
  input  in_4,
  output [7:0] out_5,
  output out_6,
  output [3:0] out_7
);

  wire and_1_out, and_2_out, and_3_out, and_4_out, and_5_out, and_6_out, and_7_out, and_8_out, and_9_out,
       and_10_out, and_11_out, and_12_out, and_13_out, and_14_out, and_15_out, and_16_out, not_1_out,
       not_2_out, not_3_out, not_4_out, not_5_out;

  not not_1 (not_1_out, in_1);
  not not_2 (not_2_out, in_2);
  not not_3 (not_3_out, in_3);
  not not_4 (not_4_out, in_4);
  and and_1 (and_1_out, not_1_out, not_3_out);
  or or_1 (out_5[5], and_1_out, in_2, in_4, and_2_out);
  and and_2 (and_2_out, in_1, in_3);
  and and_3 (and_3_out, not_1_out, not_2_out);
  or or_2 (out_5[4], and_3_out, not_3_out, and_4_out);
  and and_4 (and_4_out, in_1, in_2);
  and and_5 (and_5_out, not_1_out, not_2_out);
  or or_3 (out_5[6], and_5_out, and_6_out, and_7_out, in_4);
  and and_6 (and_6_out, in_3, not_1_out);
  and and_7 (and_7_out, not_2_out, in_3);
  and and_8 (and_8_out, in_3, not_2_out);
  or or_4 (out_5[7], and_8_out, and_9_out, and_10_out, in_4);
  and and_9 (and_9_out, in_2, not_3_out);
  and and_10 (and_10_out, in_3, not_1_out);
  and and_11 (and_11_out, not_1_out, in_2);
  or or_5 (out_5[3], and_11_out, and_12_out);
  and and_12 (and_12_out, not_1_out, not_3_out);
  and and_13 (and_13_out, in_1, not_2_out, in_3);
  and and_14 (and_14_out, in_2, not_1_out);
  or or_6 (out_5[2], and_13_out, and_14_out, and_15_out, and_16_out, in_4);
  and and_15 (and_15_out, not_3_out, in_2);
  and and_16 (and_16_out, not_3_out, not_1_out);
  or or_7 (out_5[1], not_2_out, in_1, in_3);
  _7_Segment_Display u_7_segment_display_1 (
    .g(out_5[7]), .f(out_5[6]), .a(out_5[5]), .b(out_5[4]), .e(out_5[3]), .d(out_5[2]), .c(out_5[1]));  // open: dp
  not not_5 (not_5_out, out_5[1]);
  and and_17 (out_6, not_5_out, out_5[7], out_5[6], out_5[4], out_5[5], out_5[2], out_5[3]);

  assign out_7 = {in_4, in_3, in_2, in_1};
endmodule

module bit_counter_falling_edge (
  input  in_1,
  input  in_2,
  input  [3:0] in_3,
  input  in_4,
  input  in_5,
  output [3:0] out_6
);

  wire and_1_out, and_2_out, and_3_out, and_4_out, and_5_out, and_6_out, and_7_out, and_8_out, and_9_out,
       and_10_out, and_11_out, not_1_out, not_2_out, not_3_out, not_4_out, or_1_out, or_2_out, or_3_out,
       or_4_out, or_5_out, or_6_out, or_7_out, or_8_out;

  not not_1 (not_1_out, in_3[3]);
  not not_2 (not_2_out, in_3[2]);
  not not_3 (not_3_out, in_3[1]);
  and and_1 (and_1_out, in_1, not_1_out);
  and and_2 (and_2_out, in_1, not_2_out);
  and and_3 (and_3_out, not_3_out, in_1);
  not not_4 (not_4_out, in_3[0]);
  and and_4 (and_4_out, in_1, in_3[3]);
  and and_5 (and_5_out, in_3[2], in_1);
  and and_6 (and_6_out, in_5, and_7_out, out_6[1]);
  and and_7 (and_7_out, in_5, out_6[0]);
  and and_8 (and_8_out, in_3[0], in_1);
  and and_9 (and_9_out, not_4_out, in_1);
  or or_1 (or_1_out, and_1_out, and_10_out);
  and and_10 (and_10_out, in_5, and_6_out, out_6[2]);
  or or_2 (or_2_out, and_2_out, and_6_out);
  and and_11 (and_11_out, in_1, in_3[1]);
  or or_3 (or_3_out, and_3_out, and_7_out);
  or or_4 (or_4_out, and_8_out, in_5);
  or or_5 (or_5_out, in_5, and_9_out);
  or or_6 (or_6_out, and_4_out, and_10_out);
  or or_7 (or_7_out, and_5_out, and_6_out);
  or or_8 (or_8_out, and_11_out, and_7_out);
  J_K_Flip_Flop #(.trigger("falling")) j_k_ff_1 (
    .J(or_6_out), .clk(in_4), .K(or_1_out), .Q(out_6[3]), .reset(in_2));  // open: Qn, preset, en
  J_K_Flip_Flop #(.trigger("falling")) j_k_ff_2 (
    .J(or_7_out), .clk(in_4), .K(or_2_out), .Q(out_6[2]), .reset(in_2));  // open: Qn, preset, en
  J_K_Flip_Flop #(.trigger("falling")) j_k_ff_3 (
    .J(or_8_out), .clk(in_4), .K(or_3_out), .Q(out_6[1]), .reset(in_2));  // open: Qn, preset, en
  J_K_Flip_Flop #(.trigger("falling")) j_k_ff_4 (
    .J(or_4_out), .clk(in_4), .K(or_5_out), .Q(out_6[0]), .reset(in_2));  // open: Qn, preset, en
endmodule

module decoder (
  input  in_1,
  input  in_2,
  input  in_3,
  input  in_4,
  input  in_5,
  output [15:0] out_6,
  output [3:0] out_7
);

  wire and_1_out, and_2_out, and_3_out, and_4_out, and_5_out, and_6_out, and_7_out, and_8_out, and_9_out,
       and_10_out, and_11_out, and_12_out, and_13_out, and_14_out, and_15_out, and_16_out, not_1_out,
       not_2_out, not_3_out, not_4_out;

  assign out_7[0] = in_1 ? in_2 : 1'bz;  // Controlled_Buffer controlled_buffer_1
  assign out_7[1] = in_1 ? in_3 : 1'bz;  // Controlled_Buffer controlled_buffer_2
  assign out_7[2] = in_1 ? in_4 : 1'bz;  // Controlled_Buffer controlled_buffer_3
  assign out_7[3] = in_1 ? in_5 : 1'bz;  // Controlled_Buffer controlled_buffer_4
  not not_1 (not_1_out, out_7[0]);
  not not_2 (not_2_out, out_7[1]);
  not not_3 (not_3_out, out_7[2]);
  not not_4 (not_4_out, out_7[3]);
  and and_1 (and_1_out, not_1_out, not_2_out, not_3_out, not_4_out);
  and and_2 (and_2_out, not_2_out, out_7[0], not_3_out, not_4_out);
  and and_3 (and_3_out, out_7[1], not_1_out, not_3_out, not_4_out);
  and and_4 (and_4_out, not_4_out, not_3_out, out_7[0], out_7[1]);
  and and_5 (and_5_out, out_7[2], not_1_out, not_4_out, not_2_out);
  and and_6 (and_6_out, not_4_out, out_7[2], not_2_out, out_7[0]);
  and and_7 (and_7_out, out_7[1], out_7[2], not_1_out, not_4_out);
  and and_8 (and_8_out, not_4_out, out_7[0], out_7[2], out_7[1]);
  and and_9 (and_9_out, out_7[3], not_3_out, not_2_out, not_1_out);
  and and_10 (and_10_out, out_7[3], not_3_out, not_2_out, out_7[0]);
  and and_11 (and_11_out, not_3_out, not_1_out, out_7[3], out_7[1]);
  and and_12 (and_12_out, not_3_out, out_7[3], out_7[1], out_7[0]);
  and and_13 (and_13_out, out_7[2], out_7[3], not_2_out, not_1_out);
  and and_14 (and_14_out, not_2_out, out_7[3], out_7[2], out_7[0]);
  and and_15 (and_15_out, not_1_out, out_7[3], out_7[2], out_7[1]);
  and and_16 (and_16_out, out_7[3], out_7[2], out_7[1], out_7[0]);
  and and_17 (out_6[0], in_1, and_1_out);
  and and_18 (out_6[1], in_1, and_2_out);
  and and_19 (out_6[2], in_1, and_3_out);
  and and_20 (out_6[3], in_1, and_4_out);
  and and_21 (out_6[4], in_1, and_5_out);
  and and_22 (out_6[5], in_1, and_6_out);
  and and_23 (out_6[6], in_1, and_7_out);
  and and_24 (out_6[7], and_8_out, in_1);
  and and_25 (out_6[8], and_9_out, in_1);
  and and_26 (out_6[9], and_10_out, in_1);
  and and_27 (out_6[10], and_11_out, in_1);
  and and_28 (out_6[11], and_12_out, in_1);
  and and_29 (out_6[12], and_13_out, in_1);
  and and_30 (out_6[13], and_14_out, in_1);
  and and_31 (out_6[14], and_15_out, in_1);
  and and_32 (out_6[15], and_16_out, in_1);
endmodule
