// Logisim project CPU.circ as structural Verilog: 16 circuits, main circuit main
module main (
  input  in_1,
  output [7:0] out_2,
  output [3:0] out_3,
  output [3:0] out_4,
  output [3:0] out_5,
  output [3:0] out_6,
  output [3:0] out_7,
  output [7:0] out_8,
  output [3:0] out_9,
  output [7:0] out_10,
  output [3:0] out_11,
  output [3:0] out_12,
  output [7:0] out_13
);

  wire alu_1_out_12, alu_1_out_13, alu_1_out_14, clock_1_out, decoder_2_out0, decoder_2_out1, decoder_2_out2,
       decoder_2_out3, decoder_2_out4, decoder_2_out5, decoder_2_out6, decoder_2_out7, not_1_out, not_2_out,
       or_1_out, or_2_out, or_3_out, or_4_out, or_5_out, or_6_out, or_7_out, or_8_out, or_9_out, xor_1_out;
  wire [1:1] and_1_out;
  wire [3:0] bitselector_1_out, bitselector_2_out, bitselector_3_out, bitselector_4_out,
       controlled_buffer_3_out;
  wire [4:0] decoder_1_out_6_2;
  wire [6:0] display_1_out_6, display_1_out_7, display_1_out_8, display_1_out_9, display_1_out_10,
       display_2_out_6, display_2_out_7, display_2_out_8, display_2_out_9, display_2_out_10;
  wire [7:0] number_display_2_out_3, number_display_2_out_3_2, number_display_2_out_3_3,
       number_display_2_out_3_4, rom_1_data;
  wire [15:0] decoder_1_out_6;
  wire [31:0] number_display_1_out_3, number_display_3_out_3;

  or or_1 (or_1_out, in_1, decoder_2_out7);
  decoder decoder_1 (
    .in_2(out_11[0]), .in_3(out_11[1]), .in_4(out_11[2]), .in_5(out_11[3]),
    .out_6({decoder_1_out_6[15:5], decoder_1_out_6_2[1:0], decoder_1_out_6[2:0]}), .in_1(decoder_2_out1),
    .out_7(out_9));
  xor xor_1 (xor_1_out, decoder_1_out_6[15], 1'b1);
  register_4bit register_4bit_1 (
    .in_1(1'b1), .in_5(controlled_buffer_3_out), .out_6(out_11), .in_2(clock_1_out), .in_3(decoder_2_out0));  // open: in_4
  bit_counter_falling_edge bit_counter_falling_edge_1 (
    .in_4(clock_1_out), .in_5(xor_1_out), .out_6(out_12), .in_2(or_1_out));  // open: in_1, in_3
  Decoder #(.select(4)) decoder_2 (
    .out0(decoder_2_out0), .out1(decoder_2_out1), .out2(decoder_2_out2), .out3(decoder_2_out3),
    .out4(decoder_2_out4), .out5(decoder_2_out5), .out6(decoder_2_out6), .out7(decoder_2_out7), .sel(out_12));  // open: out8, out9, out10, out11, out12, out13, out14, out15, en
  ROM #(.addrWidth(4)) rom_1 (.addr(out_4), .data(rom_1_data));  // open: sel
  RAM #(.addrWidth(4), .bus("separate")) ram_1 (
    .addr(out_7), .din(out_2), .data(out_2), .str(decoder_2_out5), .clk(clock_1_out), .ld(or_6_out));  // open: sel, clr
  not not_1 (not_1_out, clock_1_out);
  or or_2 (or_2_out, decoder_1_out_6[0], decoder_2_out0);
  or or_3 (or_3_out, decoder_2_out3, decoder_2_out0);
  or or_4 (or_4_out, decoder_2_out0, decoder_2_out3, or_6_out, decoder_2_out5);
  register_4bit register_4bit_2 (
    .in_1(or_4_out), .in_5(out_6), .out_6(out_7), .in_2(not_1_out), .in_3(or_3_out));  // open: in_4
  assign out_4 = decoder_2_out0 ? out_3 : 4'bz;  // Controlled_Buffer controlled_buffer_1
  assign out_6 = decoder_2_out0 ? bitselector_1_out : 4'bz;  // Controlled_Buffer controlled_buffer_2
  or or_5 (or_5_out, decoder_1_out_6_2[1], decoder_1_out_6_2[0], decoder_1_out_6[6], decoder_1_out_6[7], decoder_1_out_6[8], decoder_1_out_6[9], decoder_1_out_6[10]);
  assign controlled_buffer_3_out = decoder_2_out0 ? bitselector_2_out : 4'bz;  // Controlled_Buffer controlled_buffer_3
  Clock clock_1 (.out(clock_1_out));
  assign out_2 = or_2_out ? rom_1_data : 8'bz;  // Controlled_Buffer controlled_buffer_4
  assign out_6 = decoder_2_out3 ? out_5 : 4'bz;  // Controlled_Buffer controlled_buffer_5
  BitSelector #(.group(4)) bitselector_1 (.in(out_2), .out(bitselector_1_out), .sel(1'b0));
  or or_6 (or_6_out, decoder_1_out_6[2], decoder_1_out_6[1]);
  BitSelector #(.group(4)) bitselector_2 (.in(out_2), .out(bitselector_2_out), .sel(1'b1));
  or or_7 (or_7_out, decoder_2_out3, decoder_1_out_6[5]);
  or or_8 (or_8_out, decoder_2_out6, decoder_2_out5);
  bit_counter bit_counter_1 (
    .out_6(out_3), .in_3(bitselector_3_out), .in_5(decoder_2_out2), .in_1(or_7_out), .in_4(clock_1_out),
    .in_2(in_1));
  BitSelector #(.group(4)) bitselector_3 (.in(out_2), .out(bitselector_3_out), .sel(1'b0));
  register_8_bit register_8_bit_1 (
    .in_1(1'b1), .in_2(clock_1_out), .in_3(decoder_1_out_6[1]), .in_4(decoder_1_out_6[14]), .in_5(out_2),
    .out_6(out_8));
  ALU alu_1 (
    .out_11(out_10), .in_8(out_8), .in_9(out_13), .out_12(alu_1_out_12), .out_13(alu_1_out_13),
    .out_14(alu_1_out_14), .in_1(decoder_1_out_6[6]), .in_2(decoder_1_out_6[7]), .in_3(decoder_1_out_6[8]),
    .in_4(decoder_1_out_6[9]), .in_5(decoder_1_out_6_2[0]), .in_6(decoder_1_out_6_2[1]),
    .in_7(decoder_1_out_6[10]));  // open: out_10
  not not_2 (not_2_out, clock_1_out);
  register_8_bit register_8_bit_2 (
    .in_1(1'b1), .in_2(clock_1_out), .in_3(decoder_1_out_6[2]), .in_4(decoder_1_out_6[14]), .in_5(out_2),
    .out_6(out_13));
  bit_counter bit_counter_2 (
    .out_6(out_5), .in_3(bitselector_4_out), .in_5(decoder_2_out4), .in_1(decoder_1_out_6[0]),
    .in_4(clock_1_out));  // open: in_2
  BitSelector #(.group(4)) bitselector_4 (.in(out_2), .out(bitselector_4_out), .sel(1'b0));
  register_8_bit register_8_bit_3 (
    .in_1(or_8_out), .in_2(not_2_out), .in_3(or_5_out), .in_4(decoder_1_out_6[14]), .in_5(out_10),
    .out_6(out_2));
  Number_display number_display_1 (.in_2(out_13), .out_3(number_display_1_out_3), .in_1(decoder_2_out6));
  or or_9 (or_9_out, and_1_out[1], decoder_2_out6);
  Number_display number_display_2 (
    .in_2(out_2),
    .out_3({number_display_2_out_3_4, number_display_2_out_3_3, number_display_2_out_3_2, number_display_2_out_3}),
    .in_1(decoder_2_out6));
  Number_display number_display_3 (.in_2(out_8), .out_3(number_display_3_out_3), .in_1(decoder_2_out6));
  and and_1 (and_1_out[1], alu_1_out_12, decoder_1_out_6_2[1]);
  display display_1 (
    .out_9(display_1_out_9), .out_6(display_1_out_6), .out_8(display_1_out_8), .out_7(display_1_out_7),
    .out_10(display_1_out_10), .in_3(clock_1_out), .in_2(or_9_out), .in_5({{6{1'b0}}, and_1_out[1], 1'b0}),
    .in_1(decoder_2_out6), .in_4(decoder_1_out_6[14]));
  DotMatrix dotmatrix_1 (
    .col0(display_1_out_9), .col1(display_1_out_6), .col2(display_1_out_8), .col3(display_1_out_7),
    .col4(display_1_out_10));
  _7_Segment_Display u_7_segment_display_1 (
    .g(number_display_3_out_3[0]), .f(number_display_3_out_3[1]), .a(number_display_3_out_3[2]),
    .b(number_display_3_out_3[3]), .e(number_display_3_out_3[4]), .d(number_display_3_out_3[5]),
    .c(number_display_3_out_3[6]), .dp(number_display_3_out_3[7]));
  _7_Segment_Display u_7_segment_display_2 (
    .g(number_display_1_out_3[0]), .f(number_display_1_out_3[1]), .a(number_display_1_out_3[2]),
    .b(number_display_1_out_3[3]), .e(number_display_1_out_3[4]), .d(number_display_1_out_3[5]),
    .c(number_display_1_out_3[6]), .dp(number_display_1_out_3[7]));
  _7_Segment_Display u_7_segment_display_3 (
    .g(number_display_2_out_3[0]), .f(number_display_2_out_3[1]), .a(number_display_2_out_3[2]),
    .b(number_display_2_out_3[3]), .e(number_display_2_out_3[4]), .d(number_display_2_out_3[5]),
    .c(number_display_2_out_3[6]), .dp(number_display_2_out_3[7]));
  _7_Segment_Display u_7_segment_display_4 (
    .g(number_display_3_out_3[8]), .f(number_display_3_out_3[9]), .a(number_display_3_out_3[10]),
    .b(number_display_3_out_3[11]), .e(number_display_3_out_3[12]), .d(number_display_3_out_3[13]),
    .c(number_display_3_out_3[14]), .dp(number_display_3_out_3[15]));
  and and_2 (decoder_1_out_6_2[2], decoder_1_out_6[10], alu_1_out_13);
  and and_3 (decoder_1_out_6_2[3], decoder_1_out_6[10], alu_1_out_14);
  and and_4 (decoder_1_out_6_2[4], alu_1_out_12, decoder_1_out_6[10]);
  _7_Segment_Display u_7_segment_display_5 (
    .g(number_display_1_out_3[8]), .f(number_display_1_out_3[9]), .a(number_display_1_out_3[10]),
    .b(number_display_1_out_3[11]), .e(number_display_1_out_3[12]), .d(number_display_1_out_3[13]),
    .c(number_display_1_out_3[14]), .dp(number_display_1_out_3[15]));
  _7_Segment_Display u_7_segment_display_6 (
    .g(number_display_2_out_3_2[0]), .f(number_display_2_out_3_2[1]), .a(number_display_2_out_3_2[2]),
    .b(number_display_2_out_3_2[3]), .e(number_display_2_out_3_2[4]), .d(number_display_2_out_3_2[5]),
    .c(number_display_2_out_3_2[6]), .dp(number_display_2_out_3_2[7]));
  _7_Segment_Display u_7_segment_display_7 (
    .g(number_display_3_out_3[16]), .f(number_display_3_out_3[17]), .a(number_display_3_out_3[18]),
    .b(number_display_3_out_3[19]), .e(number_display_3_out_3[20]), .d(number_display_3_out_3[21]),
    .c(number_display_3_out_3[22]), .dp(number_display_3_out_3[23]));
  _7_Segment_Display u_7_segment_display_8 (
    .g(number_display_1_out_3[16]), .f(number_display_1_out_3[17]), .a(number_display_1_out_3[18]),
    .b(number_display_1_out_3[19]), .e(number_display_1_out_3[20]), .d(number_display_1_out_3[21]),
    .c(number_display_1_out_3[22]), .dp(number_display_1_out_3[23]));
  _7_Segment_Display u_7_segment_display_9 (
    .g(number_display_2_out_3_3[0]), .f(number_display_2_out_3_3[1]), .a(number_display_2_out_3_3[2]),
    .b(number_display_2_out_3_3[3]), .e(number_display_2_out_3_3[4]), .d(number_display_2_out_3_3[5]),
    .c(number_display_2_out_3_3[6]), .dp(number_display_2_out_3_3[7]));
  _7_Segment_Display u_7_segment_display_10 (
    .g(number_display_3_out_3[24]), .f(number_display_3_out_3[25]), .a(number_display_3_out_3[26]),
    .b(number_display_3_out_3[27]), .e(number_display_3_out_3[28]), .d(number_display_3_out_3[29]),
    .c(number_display_3_out_3[30]), .dp(number_display_3_out_3[31]));
  DotMatrix dotmatrix_2 (
    .col0(display_2_out_9), .col1(display_2_out_6), .col2(display_2_out_8), .col3(display_2_out_7),
    .col4(display_2_out_10));
  display display_2 (
    .out_9(display_2_out_9), .out_6(display_2_out_6), .out_8(display_2_out_8), .out_7(display_2_out_7),
    .out_10(display_2_out_10), .in_3(clock_1_out), .in_2(or_5_out), .in_5({3'b000, decoder_1_out_6_2}),
    .in_1(decoder_2_out6), .in_4(decoder_1_out_6[14]));
  _7_Segment_Display u_7_segment_display_11 (
    .g(number_display_1_out_3[24]), .f(number_display_1_out_3[25]), .a(number_display_1_out_3[26]),
    .b(number_display_1_out_3[27]), .e(number_display_1_out_3[28]), .d(number_display_1_out_3[29]),
    .c(number_display_1_out_3[30]), .dp(number_display_1_out_3[31]));
  _7_Segment_Display u_7_segment_display_12 (
    .g(number_display_2_out_3_4[0]), .f(number_display_2_out_3_4[1]), .a(number_display_2_out_3_4[2]),
    .b(number_display_2_out_3_4[3]), .e(number_display_2_out_3_4[4]), .d(number_display_2_out_3_4[5]),
    .c(number_display_2_out_3_4[6]), .dp(number_display_2_out_3_4[7]));

  // Notes on the sheet:
  //   contents of rom_1 (hex, n*v repeats v):
  //   4 11 22 30 40 60 70 80 90 a0 e0 f0
  //   8-Bit Computer
  //   Program
  //   A
  //   B
  //   Data
  //   1---LOAD A
  //   2---LOAD B
  //   3---ADD
  //   4---SUB
  //   5---JUMP
  //   6---AND
  //   7---OR
  //   8---XOR
  //   9---NOR
  //   a---Compare
  //   e---Clear
  //   f---Stop
  //   0---Initiate Data Address 
endmodule

module num_to_bi (
  input  in_1,
  input  in_2,
  input  in_3,
  input  in_4,
  input  in_5,
  input  in_6,
  input  in_7,
  input  in_8,
  input  in_9,
  input  in_10,
  input  in_11,
  output [7:0] out_12
);

  wire and_1_out, and_2_out, and_3_out, and_4_out, and_5_out, and_6_out, and_7_out, and_8_out, and_9_out,
       and_14_out, and_15_out, clock_1_out, j_k_ff_1_q, j_k_ff_1_qn, j_k_ff_2_q, j_k_ff_2_qn, not_1_out,
       not_2_out, not_3_out, not_4_out, not_5_out, not_6_out, not_7_out, not_8_out, not_9_out, not_10_out,
       not_11_out, not_12_out, not_13_out, not_14_out, not_15_out, not_16_out, not_17_out, not_18_out,
       not_19_out, not_20_out, not_21_out, not_22_out, not_23_out, not_24_out, not_25_out, not_26_out,
       not_27_out, not_28_out, not_29_out, or_1_out, or_2_out, or_3_out, or_4_out, or_5_out;
  wire [3:0] and_13_out;

  not not_1 (not_1_out, in_1);
  not not_2 (not_2_out, in_2);
  not not_3 (not_3_out, in_3);
  not not_4 (not_4_out, in_4);
  not not_5 (not_5_out, in_5);
  not not_6 (not_6_out, in_6);
  not not_7 (not_7_out, in_7);
  not not_8 (not_8_out, in_9);
  not not_9 (not_9_out, in_1);
  not not_10 (not_10_out, in_2);
  not not_11 (not_11_out, in_3);
  not not_12 (not_12_out, in_4);
  not not_13 (not_13_out, in_10);
  not not_14 (not_14_out, in_11);
  and and_1 (and_1_out, in_5, in_6, in_7, in_9);
  not not_15 (not_15_out, in_1);
  not not_16 (not_16_out, in_2);
  not not_17 (not_17_out, in_5);
  not not_18 (not_18_out, in_6);
  not not_19 (not_19_out, in_10);
  not not_20 (not_20_out, in_11);
  and and_2 (and_2_out, in_3, in_4, in_7, in_9);
  not not_21 (not_21_out, in_1);
  not not_22 (not_22_out, in_3);
  not not_23 (not_23_out, in_5);
  not not_24 (not_24_out, in_7);
  not not_25 (not_25_out, in_10);
  and and_3 (and_3_out, in_2, in_4, in_6, in_9, in_11);
  and and_4 (and_4_out, not_1_out, not_2_out, not_3_out, not_4_out, or_1_out, not_5_out, not_6_out, not_7_out, not_8_out);
  and and_5 (and_5_out, not_9_out, not_10_out, not_11_out, not_12_out, or_1_out, not_13_out, not_14_out);
  and and_6 (and_6_out, not_15_out, not_16_out, not_17_out, not_18_out, or_1_out, not_19_out, not_20_out);
  and and_7 (and_7_out, not_21_out, not_22_out, not_23_out, not_25_out, not_24_out, or_1_out);
  or or_1 (or_1_out, in_11, in_10, in_9, in_7, in_6, in_4, in_3, in_2, in_1, in_5);
  or or_2 (or_2_out, and_4_out, and_8_out);
  and and_8 (and_8_out, in_10, in_11);
  or or_3 (or_3_out, and_5_out, and_1_out);
  or or_4 (or_4_out, and_6_out, and_2_out);
  or or_5 (or_5_out, and_7_out, and_3_out);
  and and_9 (and_9_out, clock_1_out, or_1_out);
  not not_26 (not_26_out, or_2_out);
  not not_27 (not_27_out, or_3_out);
  not not_28 (not_28_out, or_4_out);
  not not_29 (not_29_out, or_5_out);
  and and_10 (and_13_out[3], or_2_out, in_8);
  and and_11 (and_13_out[2], or_3_out, in_8);
  and and_12 (and_13_out[1], or_4_out, in_8);
  and and_13 (and_13_out[0], or_5_out, in_8);
  J_K_Flip_Flop j_k_ff_1 (
    .J(j_k_ff_1_qn), .clk(and_9_out), .K(j_k_ff_2_qn), .Q(j_k_ff_1_q), .Qn(j_k_ff_1_qn));  // open: preset, en, reset
  J_K_Flip_Flop j_k_ff_2 (
    .J(j_k_ff_1_q), .clk(and_9_out), .K(j_k_ff_2_q), .Q(j_k_ff_2_q), .Qn(j_k_ff_2_qn));  // open: preset, en, reset
  // OR_Gate or_6 has open pins: in0=not_26_out, in1=not_27_out, in2=not_28_out, in3=not_29_out, out=open
  Clock clock_1 (.out(clock_1_out));
  and and_14 (and_14_out, j_k_ff_1_qn, or_1_out);
  and and_15 (and_15_out, j_k_ff_2_qn, or_1_out);
  register_4bit register_4bit_1 (
    .in_1(1'b1), .in_5(and_13_out), .out_6(out_12[3:0]), .in_2(clock_1_out), .in_3(and_14_out));  // open: in_4
  register_4bit register_4bit_2 (
    .in_1(1'b1), .in_5(and_13_out), .out_6(out_12[7:4]), .in_2(clock_1_out), .in_3(and_15_out));  // open: in_4
  ROM rom_1 (.addr(out_12));  // open: data, sel
endmodule

module register_4bit (
  input  in_1,
  input  in_2,
  input  in_3,
  input  in_4,
  input  [3:0] in_5,
  output [3:0] out_6
);

  wire controlled_buffer_1_out, controlled_buffer_2_out, controlled_buffer_3_out, controlled_buffer_4_out,
       d_ff_1_q, d_ff_2_q, d_ff_3_q, d_ff_4_q;

  assign controlled_buffer_1_out = in_3 ? in_5[3] : 1'bz;  // Controlled_Buffer controlled_buffer_1
  assign controlled_buffer_2_out = in_3 ? in_5[2] : 1'bz;  // Controlled_Buffer controlled_buffer_2
  assign controlled_buffer_3_out = in_3 ? in_5[1] : 1'bz;  // Controlled_Buffer controlled_buffer_3
  assign controlled_buffer_4_out = in_3 ? in_5[0] : 1'bz;  // Controlled_Buffer controlled_buffer_4
  D_Flip_Flop d_ff_1 (.clk(in_2), .D(controlled_buffer_1_out), .Q(d_ff_1_q), .reset(in_4));  // open: Qn, preset, en
  D_Flip_Flop d_ff_2 (.clk(in_2), .D(controlled_buffer_2_out), .Q(d_ff_2_q), .reset(in_4));  // open: Qn, preset, en
  D_Flip_Flop d_ff_3 (.clk(in_2), .D(controlled_buffer_3_out), .Q(d_ff_3_q), .reset(in_4));  // open: Qn, preset, en
  D_Flip_Flop d_ff_4 (.clk(in_2), .D(controlled_buffer_4_out), .Q(d_ff_4_q), .reset(in_4));  // open: Qn, preset, en
  assign out_6[3] = in_1 ? d_ff_1_q : 1'bz;  // Controlled_Buffer controlled_buffer_5
  assign out_6[2] = in_1 ? d_ff_2_q : 1'bz;  // Controlled_Buffer controlled_buffer_6
  assign out_6[1] = in_1 ? d_ff_3_q : 1'bz;  // Controlled_Buffer controlled_buffer_7
  assign out_6[0] = in_1 ? d_ff_4_q : 1'bz;  // Controlled_Buffer controlled_buffer_8
endmodule

module ALU (
  input  in_1,
  input  in_2,
  input  in_3,
  input  in_4,
  input  in_5,
  input  in_6,
  input  in_7,
  input  [7:0] in_8,
  input  [7:0] in_9,
  output [2:0] out_10,
  output [7:0] out_11,
  output out_12,
  output out_13,
  output out_14
);

  wire alu_1bit_arthi_1_out_8, alu_1bit_arthi_2_out_8, alu_1bit_arthi_3_out_8, alu_1bit_arthi_4_out_8,
       alu_1bit_arthi_5_out_8, alu_1bit_arthi_6_out_8, alu_1bit_arthi_7_out_8, and_1_out,
       bi_comparator_1_out_6, bi_comparator_1_out_7, bi_comparator_1_out_8, n2s_complement_1_out_5,
       not_1_out, or_1_out;
  wire [3:0] alu_1bit_arthi_1_out_7, alu_1bit_arthi_5_out_7;

  Bi_comparator bi_comparator_1 (
    .in_1(in_8[3:0]), .in_2(in_9[3:0]), .in_3(1'b0), .in_4(1'b1), .in_5(1'b0), .out_6(bi_comparator_1_out_6),
    .out_7(bi_comparator_1_out_7), .out_8(bi_comparator_1_out_8));
  Bi_comparator bi_comparator_2 (
    .in_1(in_8[7:4]), .in_2(in_9[7:4]), .in_3(bi_comparator_1_out_8), .in_4(bi_comparator_1_out_7),
    .in_5(bi_comparator_1_out_6), .out_6(out_14), .out_7(out_13), .out_8(out_12));
  and and_1 (and_1_out, in_6, out_12);
  or or_1 (or_1_out, in_6, 1'b0);
  coder_circuit coder_circuit_1 (.out_2(out_10), .in_1({in_7, in_6, in_5, in_4, in_3, in_2, in_1}));
  ALU_1bit_Arthi alu_1bit_arthi_1 (
    .in_2(in_8[0]), .in_3(in_9[0]), .in_4(in_6), .out_7(alu_1bit_arthi_1_out_7[0]),
    .out_8(alu_1bit_arthi_1_out_8), .in_1(out_10), .in_5(or_1_out), .in_6({out_14, out_13, out_12}));  // open: out_9
  ALU_1bit_Arthi alu_1bit_arthi_2 (
    .in_2(in_8[1]), .in_3(in_9[1]), .in_4(in_6), .out_7(alu_1bit_arthi_1_out_7[1]),
    .out_8(alu_1bit_arthi_2_out_8), .in_1(out_10), .in_5(alu_1bit_arthi_1_out_8),
    .in_6({out_14, out_13, out_12}));  // open: out_9
  ALU_1bit_Arthi alu_1bit_arthi_3 (
    .in_2(in_8[2]), .in_3(in_9[2]), .in_4(in_6), .out_7(alu_1bit_arthi_1_out_7[2]),
    .out_8(alu_1bit_arthi_3_out_8), .in_1(out_10), .in_5(alu_1bit_arthi_2_out_8),
    .in_6({out_14, out_13, out_12}));  // open: out_9
  ALU_1bit_Arthi alu_1bit_arthi_4 (
    .in_2(in_8[3]), .in_3(in_9[3]), .in_4(in_6), .out_7(alu_1bit_arthi_1_out_7[3]),
    .out_8(alu_1bit_arthi_4_out_8), .in_1(out_10), .in_5(alu_1bit_arthi_3_out_8),
    .in_6({out_14, out_13, out_12}));  // open: out_9
  ALU_1bit_Arthi alu_1bit_arthi_5 (
    .in_2(in_8[4]), .in_3(in_9[4]), .in_4(in_6), .out_7(alu_1bit_arthi_5_out_7[0]),
    .out_8(alu_1bit_arthi_5_out_8), .in_1(out_10), .in_5(alu_1bit_arthi_4_out_8),
    .in_6({out_14, out_13, out_12}));  // open: out_9
  ALU_1bit_Arthi alu_1bit_arthi_6 (
    .in_2(in_8[5]), .in_3(in_9[5]), .in_4(in_6), .out_7(alu_1bit_arthi_5_out_7[1]),
    .out_8(alu_1bit_arthi_6_out_8), .in_1(out_10), .in_5(alu_1bit_arthi_5_out_8),
    .in_6({out_14, out_13, out_12}));  // open: out_9
  ALU_1bit_Arthi alu_1bit_arthi_7 (
    .in_2(in_8[6]), .in_3(in_9[6]), .in_4(in_6), .out_7(alu_1bit_arthi_5_out_7[2]),
    .out_8(alu_1bit_arthi_7_out_8), .in_1(out_10), .in_5(alu_1bit_arthi_6_out_8),
    .in_6({out_14, out_13, out_12}));  // open: out_9
  ALU_1bit_Arthi alu_1bit_arthi_8 (
    .in_2(in_8[7]), .in_3(in_9[7]), .in_4(in_6), .out_7(alu_1bit_arthi_5_out_7[3]), .in_1(out_10),
    .in_5(alu_1bit_arthi_7_out_8), .in_6({out_14, out_13, out_12}));  // open: out_8, out_9
  not not_1 (not_1_out, and_1_out);
  assign out_11 = not_1_out ? {alu_1bit_arthi_5_out_7, alu_1bit_arthi_1_out_7} : 8'bz;  // Controlled_Buffer controlled_buffer_1
  _2s_complement u_2s_complement_1 (
    .in_1(alu_1bit_arthi_1_out_7), .out_4(out_11[3:0]), .in_3(1'b1), .out_5(n2s_complement_1_out_5),
    .in_2(and_1_out));
  _2s_complement u_2s_complement_2 (
    .in_1(alu_1bit_arthi_5_out_7), .out_4(out_11[7:4]), .in_3(n2s_complement_1_out_5), .in_2(and_1_out));  // open: out_5
endmodule

module full_adder (
  input  in_1,
  input  in_2,
  input  in_3,
  output out_4,
  output out_5
);

  wire and_1_out, and_2_out, xor_1_out;

  and and_1 (and_1_out, in_2, in_1);
  xor xor_1 (xor_1_out, in_1, in_2);
  xor xor_2 (out_4, and_1_out, and_2_out);
  and and_2 (and_2_out, in_3, xor_1_out);
  xor xor_3 (out_5, xor_1_out, in_3);
endmodule

module register_8_bit (
  input  in_1,
  input  in_2,
  input  in_3,
  input  in_4,
  input  [7:0] in_5,
  output [7:0] out_6
);

  wire d_ff_1_q, d_ff_2_q, d_ff_3_q, d_ff_4_q, d_ff_5_q, d_ff_6_q, d_ff_7_q, d_ff_8_q;
  wire [7:0] controlled_buffer_1_out;

  assign controlled_buffer_1_out = in_3 ? in_5 : 8'bz;  // Controlled_Buffer controlled_buffer_1
  D_Flip_Flop d_ff_1 (
    .clk(in_2), .D(controlled_buffer_1_out[7]), .Q(d_ff_1_q), .en(1'b1), .reset(in_4));  // open: Qn, preset
  D_Flip_Flop d_ff_2 (
    .clk(in_2), .D(controlled_buffer_1_out[6]), .Q(d_ff_2_q), .en(1'b1), .reset(in_4));  // open: Qn, preset
  D_Flip_Flop d_ff_3 (
    .clk(in_2), .D(controlled_buffer_1_out[5]), .Q(d_ff_3_q), .en(1'b1), .reset(in_4));  // open: Qn, preset
  D_Flip_Flop d_ff_4 (
    .clk(in_2), .D(controlled_buffer_1_out[4]), .Q(d_ff_4_q), .en(1'b1), .reset(in_4));  // open: Qn, preset
  D_Flip_Flop d_ff_5 (
    .clk(in_2), .D(controlled_buffer_1_out[3]), .Q(d_ff_5_q), .en(1'b1), .reset(in_4));  // open: Qn, preset
  D_Flip_Flop d_ff_6 (
    .clk(in_2), .D(controlled_buffer_1_out[2]), .Q(d_ff_6_q), .en(1'b1), .reset(in_4));  // open: Qn, preset
  D_Flip_Flop d_ff_7 (
    .clk(in_2), .D(controlled_buffer_1_out[1]), .Q(d_ff_7_q), .en(1'b1), .reset(in_4));  // open: Qn, preset
  D_Flip_Flop d_ff_8 (
    .clk(in_2), .D(controlled_buffer_1_out[0]), .Q(d_ff_8_q), .en(1'b1), .reset(in_4));  // open: Qn, preset
  assign out_6[7] = in_1 ? d_ff_1_q : 1'bz;  // Controlled_Buffer controlled_buffer_2
  assign out_6[6] = in_1 ? d_ff_2_q : 1'bz;  // Controlled_Buffer controlled_buffer_3
  assign out_6[5] = in_1 ? d_ff_3_q : 1'bz;  // Controlled_Buffer controlled_buffer_4
  assign out_6[4] = in_1 ? d_ff_4_q : 1'bz;  // Controlled_Buffer controlled_buffer_5
  assign out_6[3] = in_1 ? d_ff_5_q : 1'bz;  // Controlled_Buffer controlled_buffer_6
  assign out_6[2] = in_1 ? d_ff_6_q : 1'bz;  // Controlled_Buffer controlled_buffer_7
  assign out_6[1] = in_1 ? d_ff_7_q : 1'bz;  // Controlled_Buffer controlled_buffer_8
  assign out_6[0] = in_1 ? d_ff_8_q : 1'bz;  // Controlled_Buffer controlled_buffer_9
endmodule

module calculator1 (
  input  Program,
  input  in_2,
  input  A,
  input  B,
  input  in_5,
  output [3:0] out_6,
  output [7:0] out_7,
  output [3:0] out_8,
  output [7:0] out_9,
  output [7:0] out_10,
  output [7:0] out_11,
  output [3:0] out_12,
  output [7:0] out_13,
  output [3:0] out_14,
  output [3:0] out_15
);

  wire _6_out, _7_out, _8_out, _9_out, bit_counter_falling_edge_1_p3, bit_counter_falling_edge_1_p4,
       decoder_1_p7, decoder_2_out0, decoder_2_out2, decoder_2_out3, or_1_out, or_2_out, or_3_out;
  wire [3:0] bitselector_1_out, controlled_buffer_1_out, decoder_1_p1, register_4bit_1_out_6;
  wire [7:0] controlled_buffer_2_out, decoder_1_p5, rom_2_data, rom_3_data, rom_4_data;

  Button _7 (.out(_7_out));
  Button _8 (.out(_8_out));
  Button _5 (.out(_8_out));
  Button _4 (.out(_8_out));
  Button _2 (.out(_8_out));
  Button _1 (.out(_8_out));
  Button _0 (.out(_8_out));
  Button _9 (.out(_9_out));
  Button _6 (.out(_6_out));
  Button _3 (.out(_8_out));
  num_to_hexa num_to_hexa_1 (
    .in_1(_8_out), .in_2(_8_out), .in_3(_8_out), .in_4(_8_out), .in_5(_8_out), .in_6(_8_out), .in_7(_8_out),
    .in_8(_8_out), .in_9(_8_out), .in_10(_8_out));  // open: out_12, out_11
  // decoder decoder_1: pin names not known; wires that end beside it: decoder_1_p1[0], decoder_1_p1[1], decoder_1_p1[2], decoder_1_p1[3], decoder_1_p5, out_12, decoder_1_p7
  ROM #(.addrWidth(4), .dataWidth(4)) rom_1 (.addr(controlled_buffer_1_out), .data(decoder_1_p1));  // open: sel
  // bit_counter_falling_edge bit_counter_falling_edge_1: pin names not known; wires that end beside it: in_5, 1'b1, bit_counter_falling_edge_1_p3, bit_counter_falling_edge_1_p4, out_15
  RAM #(.addrWidth(4), .bus("separate")) ram_1 (
    .addr(register_4bit_1_out_6), .data(out_7), .str(1'b0), .clk(bit_counter_falling_edge_1_p4), .ld(or_2_out));  // open: din, sel, clr
  Decoder #(.select(4)) decoder_2 (
    .out0(decoder_2_out0), .out1(decoder_1_p7), .out2(decoder_2_out2), .out3(decoder_2_out3),
    .out4(bit_counter_falling_edge_1_p3), .sel(out_15));  // open: out5, out6, out7, out8, out9, out10, out11, out12, out13, out14, out15, en
  RAM #(.addrWidth(4), .bus("separate")) ram_2 (
    .addr(out_6), .data(out_7), .str(1'b0), .clk(bit_counter_falling_edge_1_p4), .ld(decoder_2_out0));  // open: din, sel, clr
  register_4bit register_4bit_1 (
    .in_1(or_1_out), .in_5(bitselector_1_out), .out_6(register_4bit_1_out_6),
    .in_2(bit_counter_falling_edge_1_p4), .in_3(decoder_2_out0));  // open: in_4
  Clock clock_1 (.out(bit_counter_falling_edge_1_p4));
  or or_1 (or_1_out, decoder_2_out0, or_2_out);
  assign controlled_buffer_1_out = decoder_2_out0 ? out_14 : 4'bz;  // Controlled_Buffer controlled_buffer_1
  BitSelector #(.group(4)) bitselector_1 (.in(out_7), .out(bitselector_1_out), .sel(1'b0));
  or or_2 (or_2_out, decoder_1_p5[2], decoder_1_p5[1]);
  BitSelector #(.group(4)) bitselector_2 (.in(out_7), .out(out_14), .sel(1'b1));
  assign controlled_buffer_2_out = decoder_2_out2 ? out_7 : 8'bz;  // Controlled_Buffer controlled_buffer_2
  // ALU alu_1: pin names not known; wires that end beside it: decoder_1_p5[1], out_11, out_13, out_7
  ROM rom_2 (.addr(controlled_buffer_2_out), .data(rom_2_data));  // open: sel
  // bit_counter bit_counter_1: pin names not known; wires that end beside it: in_2, decoder_2_out3, Program, bit_counter_falling_edge_1_p4, out_6
  register_8_bit register_8_bit_1 (
    .in_1(1'b1), .in_2(bit_counter_falling_edge_1_p4), .in_3(decoder_1_p5[1]), .in_4(A), .in_5(out_7),
    .out_6(out_11));
  or or_3 (or_3_out, decoder_1_p5[4], decoder_1_p5[3]);
  register_8_bit register_8_bit_2 (
    .in_1(1'b1), .in_2(bit_counter_falling_edge_1_p4), .in_3(decoder_1_p5[2]), .in_4(B), .in_5(out_7),
    .out_6(out_13));
  ROM #(.addrWidth(4)) rom_3 (.addr(rom_2_data[3:0]), .data(rom_3_data));  // open: sel
  ROM #(.addrWidth(4)) rom_4 (.addr(rom_2_data[7:4]), .data(rom_4_data));  // open: sel
  _7_Segment_Display u_7_segment_display_1 (
    .g(rom_4_data[0]), .f(rom_4_data[1]), .a(rom_4_data[2]), .b(rom_4_data[3]), .e(rom_4_data[4]),
    .d(rom_4_data[5]), .c(rom_4_data[6]), .dp(rom_4_data[7]));
  _7_Segment_Display u_7_segment_display_2 (
    .g(rom_3_data[0]), .f(rom_3_data[1]), .a(rom_3_data[2]), .b(rom_3_data[3]), .e(rom_3_data[4]),
    .d(rom_3_data[5]), .c(rom_3_data[6]), .dp(rom_3_data[7]));

  assign out_8 = out_6;
  assign out_9 = out_7;
  assign out_10 = out_7;

  // Notes on the sheet:
  //   contents of rom_1 (hex, n*v repeats v):
  //   0 1 2 3 4
  //   ALU
  //   contents of rom_2 (hex, n*v repeats v):
  //   0 1 2 3 4 5 6 7 8 9 10 11 12 13 14 15 16 17 18 19 20 21 22 23 24 25 26 27 28 29 30 31 32 33 34 35 36
  //   37 38 39 40 41 42 43 44 45 46 47 48 49 50 51 52 53 54 55 56 57 58 59 60 61 62 63 64 65 66 67 68 69
  //   70 71 72 73 74 75 76 77 78 79 80 81 82 83 84 85 86 87 88 89 90 91 92 93 94 95 96 97 98 99 0 1 2 3 4
  //   5 6 7 8 9 10 11 12 13 14 15 16 17 18 19 20 21 22 23 24 25 26 27 28 29 30 31 32 33 34 35 36 37 38 39
  //   40 41 42 43 44 45 46 47 48 49 50 51 52 53 54 55 56 57 58 59 60 61 62 63 64 65 66 67 68 69 70 71 72
  //   73 74 75 76 77 78 79 80 81 82 83 84 85 86 87 88 89 90 91 92 93 94 95 96 97 98 99 0 1 2 3 4 5 6 7 8 9
  //   10 11 12 13 14 15 16 17 18 19 20 21 22 23 24 25 26 27 28 29 30 31 32 33 34 35 36 37 38 39 40 41 42
  //   43 44 45 46 47 48 49 50 51 52 53 54
  //   contents of rom_3 (hex, n*v repeats v):
  //   7e 48 3d 6d 4b 67 77 4c 7f 6f 7e 48 3d 6d 4b 67
  //   contents of rom_4 (hex, n*v repeats v):
  //   7e 48 3d 6d 4b 67 77 4c 7f 6f 7e 48 3d 6d 4b 67
  //   0010 LOAD B
  //   0011 ADD--- ADDER-EN 
  //   0001 LOAD---ADR-OUT  MEM-IN
  //   0100SUB--- ADDER-EN  SUB-EN
endmodule

module num_to_hexa (
  input  in_1,
  input  in_2,
  input  in_3,
  input  in_4,
  input  in_5,
  input  in_6,
  input  in_7,
  input  in_8,
  input  in_9,
  input  in_10,
  output [3:0] out_11,
  output [3:0] out_12
);

  wire and_1_out, and_2_out, and_3_out, and_4_out, and_5_out, and_6_out, and_7_out, and_8_out,
       bitselector_1_out, bitselector_2_out, clock_1_out, counter_1_q, decoder_1_out0, decoder_1_out1,
       not_1_out, not_2_out, not_3_out, not_4_out, not_5_out, not_6_out, not_7_out, not_8_out, not_9_out,
       not_10_out, not_11_out, not_12_out, not_13_out, not_14_out, not_15_out, not_16_out, not_17_out,
       not_18_out, not_19_out, not_20_out, not_21_out, not_22_out, not_23_out, not_24_out, not_25_out,
       or_1_out;
  wire [3:0] or_5_out;

  not not_1 (not_1_out, in_1);
  not not_2 (not_2_out, in_2);
  not not_3 (not_3_out, in_3);
  not not_4 (not_4_out, in_4);
  not not_5 (not_5_out, in_5);
  not not_6 (not_6_out, in_6);
  not not_7 (not_7_out, in_7);
  not not_8 (not_8_out, in_8);
  not not_9 (not_9_out, in_1);
  not not_10 (not_10_out, in_2);
  not not_11 (not_11_out, in_3);
  not not_12 (not_12_out, in_4);
  not not_13 (not_13_out, in_9);
  not not_14 (not_14_out, in_10);
  and and_1 (and_1_out, in_5, in_6, in_7, in_8);
  not not_15 (not_15_out, in_1);
  not not_16 (not_16_out, in_2);
  not not_17 (not_17_out, in_5);
  not not_18 (not_18_out, in_6);
  not not_19 (not_19_out, in_9);
  not not_20 (not_20_out, in_10);
  and and_2 (and_2_out, in_3, in_4, in_7, in_8);
  and and_3 (and_3_out, not_1_out, not_2_out, not_3_out, not_4_out, or_1_out, not_5_out, not_6_out, not_7_out, not_8_out);
  and and_4 (and_4_out, not_9_out, not_10_out, not_11_out, not_12_out, or_1_out, not_13_out, not_14_out);
  and and_5 (and_5_out, not_15_out, not_16_out, not_17_out, not_18_out, or_1_out, not_19_out, not_20_out);
  not not_21 (not_21_out, in_1);
  not not_22 (not_22_out, in_3);
  not not_23 (not_23_out, in_5);
  not not_24 (not_24_out, in_7);
  and and_6 (and_6_out, not_21_out, not_22_out, not_23_out, not_25_out, not_24_out, or_1_out);
  not not_25 (not_25_out, in_9);
  and and_7 (and_7_out, in_2, in_4, in_6, in_8, in_10);
  or or_1 (or_1_out, in_10, in_9, in_8, in_7, in_6, in_4, in_3, in_2, in_1, in_5);
  Counter #(.width(1), .max('h1)) counter_1 (
    .count(or_1_out), .Q(counter_1_q), .clk(clock_1_out));  // open: load, D, carry, clr
  or or_2 (or_5_out[3], and_3_out, and_8_out);
  and and_8 (and_8_out, in_9, in_10);
  or or_3 (or_5_out[2], and_4_out, and_1_out);
  or or_4 (or_5_out[1], and_5_out, and_2_out);
  or or_5 (or_5_out[0], and_6_out, and_7_out);
  Decoder decoder_1 (.out0(decoder_1_out0), .out1(decoder_1_out1), .sel(counter_1_q));  // open: en
  BitSelector #(.width(1)) bitselector_1 (.in(or_1_out), .out(bitselector_1_out), .sel(decoder_1_out0));
  BitSelector #(.width(1)) bitselector_2 (.in(or_1_out), .out(bitselector_2_out), .sel(decoder_1_out1));
  Clock clock_1 (.out(clock_1_out));
  register_4bit register_4bit_1 (
    .in_1(1'b1), .in_5(or_5_out), .out_6(out_12), .in_2(clock_1_out), .in_3(bitselector_1_out));  // open: in_4
  register_4bit register_4bit_2 (
    .in_1(1'b1), .in_5(or_5_out), .out_6(out_11), .in_2(clock_1_out), .in_3(bitselector_2_out));  // open: in_4
  ROM rom_1 (.addr({out_11, out_12}));  // open: data, sel
endmodule

module display (
  input  in_1,
  input  in_2,
  input  in_3,
  input  in_4,
  input  [7:0] in_5,
  output [6:0] out_6,
  output [6:0] out_7,
  output [6:0] out_8,
  output [6:0] out_9,
  output [6:0] out_10
);

  wire [6:0] controlled_buffer_1_out, controlled_buffer_2_out, controlled_buffer_3_out,
       controlled_buffer_4_out, controlled_buffer_5_out, controlled_buffer_6_out, controlled_buffer_7_out,
       controlled_buffer_8_out, controlled_buffer_9_out, controlled_buffer_10_out, controlled_buffer_11_out,
       controlled_buffer_12_out, controlled_buffer_13_out, controlled_buffer_14_out,
       controlled_buffer_15_out, controlled_buffer_16_out, controlled_buffer_17_out,
       controlled_buffer_18_out, controlled_buffer_19_out, controlled_buffer_20_out,
       controlled_buffer_21_out, controlled_buffer_22_out, controlled_buffer_23_out,
       controlled_buffer_24_out, controlled_buffer_25_out;
  wire [7:0] register_8_bit_1_out_6;

  register_8_bit register_8_bit_1 (
    .in_1(in_1), .in_2(in_3), .in_3(in_2), .in_4(in_4), .in_5(in_5), .out_6(register_8_bit_1_out_6));
  assign controlled_buffer_1_out = register_8_bit_1_out_6[2] ? 7'b0010100 : 7'bz;  // Controlled_Buffer controlled_buffer_1
  assign controlled_buffer_2_out = register_8_bit_1_out_6[3] ? 7'b0100010 : 7'bz;  // Controlled_Buffer controlled_buffer_2
  assign controlled_buffer_3_out = register_8_bit_1_out_6[4] ? 7'b0001000 : 7'bz;  // Controlled_Buffer controlled_buffer_3
  assign controlled_buffer_4_out = register_8_bit_1_out_6[0] ? 7'b0001000 : 7'bz;  // Controlled_Buffer controlled_buffer_4
  assign controlled_buffer_5_out = register_8_bit_1_out_6[0] ? 7'b0001000 : 7'bz;  // Controlled_Buffer controlled_buffer_5
  assign controlled_buffer_6_out = register_8_bit_1_out_6[0] ? 7'b0111110 : 7'bz;  // Controlled_Buffer controlled_buffer_6
  assign controlled_buffer_7_out = register_8_bit_1_out_6[0] ? 7'b0001000 : 7'bz;  // Controlled_Buffer controlled_buffer_7
  assign controlled_buffer_8_out = register_8_bit_1_out_6[0] ? 7'b0001000 : 7'bz;  // Controlled_Buffer controlled_buffer_8
  assign controlled_buffer_9_out = register_8_bit_1_out_6[1] ? 7'b0001000 : 7'bz;  // Controlled_Buffer controlled_buffer_9
  assign controlled_buffer_10_out = register_8_bit_1_out_6[1] ? 7'b0001000 : 7'bz;  // Controlled_Buffer controlled_buffer_10
  assign controlled_buffer_11_out = register_8_bit_1_out_6[1] ? 7'b0001000 : 7'bz;  // Controlled_Buffer controlled_buffer_11
  assign controlled_buffer_12_out = register_8_bit_1_out_6[1] ? 7'b0001000 : 7'bz;  // Controlled_Buffer controlled_buffer_12
  assign controlled_buffer_13_out = register_8_bit_1_out_6[1] ? 7'b0001000 : 7'bz;  // Controlled_Buffer controlled_buffer_13
  assign controlled_buffer_14_out = register_8_bit_1_out_6[2] ? 7'b0010100 : 7'bz;  // Controlled_Buffer controlled_buffer_14
  assign controlled_buffer_15_out = register_8_bit_1_out_6[2] ? 7'b0010100 : 7'bz;  // Controlled_Buffer controlled_buffer_15
  assign controlled_buffer_16_out = register_8_bit_1_out_6[2] ? 7'b0010100 : 7'bz;  // Controlled_Buffer controlled_buffer_16
  assign controlled_buffer_17_out = register_8_bit_1_out_6[2] ? 7'b0010100 : 7'bz;  // Controlled_Buffer controlled_buffer_17
  assign controlled_buffer_18_out = register_8_bit_1_out_6[3] ? 7'b0100010 : 7'bz;  // Controlled_Buffer controlled_buffer_18
  assign controlled_buffer_19_out = register_8_bit_1_out_6[3] ? 7'b0010100 : 7'bz;  // Controlled_Buffer controlled_buffer_19
  assign controlled_buffer_20_out = register_8_bit_1_out_6[3] ? 7'b0010100 : 7'bz;  // Controlled_Buffer controlled_buffer_20
  assign controlled_buffer_21_out = register_8_bit_1_out_6[3] ? 7'b0001000 : 7'bz;  // Controlled_Buffer controlled_buffer_21
  assign controlled_buffer_22_out = register_8_bit_1_out_6[4] ? 7'b0010100 : 7'bz;  // Controlled_Buffer controlled_buffer_22
  assign controlled_buffer_23_out = register_8_bit_1_out_6[4] ? 7'b0010100 : 7'bz;  // Controlled_Buffer controlled_buffer_23
  assign controlled_buffer_24_out = register_8_bit_1_out_6[4] ? 7'b0100010 : 7'bz;  // Controlled_Buffer controlled_buffer_24
  assign controlled_buffer_25_out = register_8_bit_1_out_6[4] ? 7'b0100010 : 7'bz;  // Controlled_Buffer controlled_buffer_25
  assign out_9 = controlled_buffer_1_out | controlled_buffer_4_out | controlled_buffer_3_out | controlled_buffer_9_out | controlled_buffer_2_out;  // OR_Gate or_1, 7 bits wide
  assign out_6 = controlled_buffer_14_out | controlled_buffer_5_out | controlled_buffer_22_out | controlled_buffer_10_out | controlled_buffer_18_out;  // OR_Gate or_2, 7 bits wide
  assign out_8 = controlled_buffer_15_out | controlled_buffer_6_out | controlled_buffer_23_out | controlled_buffer_11_out | controlled_buffer_19_out;  // OR_Gate or_3, 7 bits wide
  assign out_7 = controlled_buffer_16_out | controlled_buffer_7_out | controlled_buffer_24_out | controlled_buffer_12_out | controlled_buffer_20_out;  // OR_Gate or_4, 7 bits wide
  assign out_10 = controlled_buffer_8_out | controlled_buffer_17_out | controlled_buffer_25_out | controlled_buffer_13_out | controlled_buffer_21_out;  // OR_Gate or_5, 7 bits wide
  DotMatrix dotmatrix_1 (.col0(out_9), .col1(out_6), .col2(out_8), .col3(out_7), .col4(out_10));
endmodule

module multiply (
  input  [7:0] in_1,
  input  [7:0] in_2,
  input  in_3,
  output [15:0] out_4
);

  wire and_1_out, and_2_out, and_3_out, and_4_out, and_5_out, and_6_out, and_7_out, and_8_out, and_9_out,
       and_10_out, and_11_out, and_12_out, and_13_out, and_14_out, and_15_out, and_16_out, and_17_out,
       and_18_out, and_19_out, and_20_out, and_21_out, and_22_out, and_23_out, and_24_out, and_25_out,
       and_26_out, and_27_out, and_28_out, and_29_out, and_30_out, and_31_out, and_32_out, and_33_out,
       and_34_out, and_35_out, and_36_out, and_37_out, and_38_out, and_39_out, and_40_out, and_41_out,
       and_42_out, and_43_out, and_44_out, and_45_out, and_46_out, and_47_out, and_48_out, and_49_out,
       and_50_out, and_51_out, and_52_out, and_53_out, and_54_out, and_55_out, and_56_out, and_57_out,
       and_58_out, and_59_out, and_60_out, and_61_out, and_62_out, and_63_out, full_adder_1_out_4,
       full_adder_1_out_5, full_adder_3_out_4, full_adder_4_out_4, full_adder_4_out_5, full_adder_5_out_4,
       full_adder_5_out_5, full_adder_6_out_4, full_adder_6_out_5, full_adder_8_out_4, full_adder_8_out_5,
       full_adder_9_out_4, full_adder_9_out_5, full_adder_10_out_4, full_adder_10_out_5, full_adder_11_out_5,
       full_adder_12_out_4, full_adder_12_out_5, full_adder_13_out_5, full_adder_14_out_4,
       full_adder_15_out_4, full_adder_15_out_5, full_adder_16_out_4, full_adder_16_out_5,
       full_adder_17_out_4, full_adder_17_out_5, full_adder_18_out_4, full_adder_18_out_5,
       full_adder_19_out_5, full_adder_20_out_4, full_adder_20_out_5, full_adder_21_out_5,
       full_adder_23_out_4, full_adder_24_out_4, full_adder_24_out_5, full_adder_25_out_5,
       full_adder_26_out_4, full_adder_26_out_5, full_adder_27_out_5, full_adder_28_out_4,
       full_adder_28_out_5, full_adder_29_out_5, full_adder_30_out_5, full_adder_31_out_4,
       full_adder_31_out_5, full_adder_33_out_5, full_adder_34_out_4, full_adder_34_out_5,
       full_adder_35_out_5, full_adder_36_out_4, full_adder_36_out_5, full_adder_37_out_4,
       full_adder_37_out_5, full_adder_38_out_5, full_adder_39_out_4, full_adder_40_out_5,
       full_adder_41_out_4, full_adder_42_out_4, full_adder_42_out_5, full_adder_43_out_5,
       full_adder_44_out_4, full_adder_44_out_5, full_adder_45_out_5, full_adder_46_out_4,
       full_adder_46_out_5, full_adder_47_out_5, full_adder_48_out_4, full_adder_49_out_4,
       full_adder_49_out_5, full_adder_50_out_5, full_adder_51_out_4, full_adder_52_out_5,
       full_adder_53_out_4, full_adder_54_out_5, full_adder_55_out_4, full_adder_56_out_4;
  wire [15:0] and_64_out;

  and and_1 (and_1_out, in_1[6], in_2[7]);
  full_adder full_adder_1 (
    .out_4(full_adder_1_out_4), .out_5(full_adder_1_out_5), .in_1(and_1_out), .in_3(full_adder_6_out_4),
    .in_2(full_adder_5_out_4));
  and and_2 (and_2_out, in_1[7], in_2[6]);
  and and_3 (and_3_out, in_1[7], in_2[7]);
  full_adder full_adder_2 (
    .out_4(and_64_out[15]), .out_5(and_64_out[14]), .in_1(and_3_out), .in_3(full_adder_3_out_4),
    .in_2(full_adder_1_out_4));
  full_adder full_adder_3 (
    .out_4(full_adder_3_out_4), .out_5(and_64_out[13]), .in_1(and_2_out), .in_3(full_adder_3_out_4),
    .in_2(full_adder_1_out_5));
  full_adder full_adder_4 (
    .out_4(full_adder_4_out_4), .out_5(full_adder_4_out_5), .in_1(and_8_out), .in_3(full_adder_9_out_4),
    .in_2(full_adder_8_out_4));
  and and_4 (and_4_out, in_1[5], in_2[7]);
  full_adder full_adder_5 (
    .out_4(full_adder_5_out_4), .out_5(full_adder_5_out_5), .in_1(and_4_out), .in_3(full_adder_10_out_4),
    .in_2(full_adder_4_out_4));
  and and_5 (and_5_out, in_1[6], in_2[6]);
  full_adder full_adder_6 (
    .out_4(full_adder_6_out_4), .out_5(full_adder_6_out_5), .in_1(and_5_out), .in_3(full_adder_6_out_4),
    .in_2(full_adder_5_out_5));
  and and_6 (and_6_out, in_1[7], in_2[5]);
  full_adder full_adder_7 (
    .out_4(full_adder_3_out_4), .out_5(and_64_out[12]), .in_1(and_6_out), .in_3(full_adder_14_out_4),
    .in_2(full_adder_6_out_5));
  and and_7 (and_7_out, in_1[3], in_2[7]);
  full_adder full_adder_8 (
    .out_4(full_adder_8_out_4), .out_5(full_adder_8_out_5), .in_1(and_7_out), .in_3(full_adder_18_out_4),
    .in_2(full_adder_17_out_4));
  and and_8 (and_8_out, in_1[4], in_2[7]);
  and and_9 (and_9_out, in_1[4], in_2[6]);
  full_adder full_adder_9 (
    .out_4(full_adder_9_out_4), .out_5(full_adder_9_out_5), .in_1(and_9_out), .in_3(full_adder_9_out_4),
    .in_2(full_adder_8_out_5));
  and and_10 (and_10_out, in_1[5], in_2[5]);
  and and_11 (and_11_out, in_1[5], in_2[6]);
  full_adder full_adder_10 (
    .out_4(full_adder_10_out_4), .out_5(full_adder_10_out_5), .in_1(and_10_out), .in_3(full_adder_20_out_4),
    .in_2(full_adder_9_out_5));
  full_adder full_adder_11 (
    .out_4(full_adder_10_out_4), .out_5(full_adder_11_out_5), .in_1(and_11_out), .in_3(full_adder_10_out_4),
    .in_2(full_adder_4_out_5));
  and and_12 (and_12_out, in_1[6], in_2[5]);
  full_adder full_adder_12 (
    .out_4(full_adder_12_out_4), .out_5(full_adder_12_out_5), .in_1(and_20_out), .in_3(full_adder_12_out_4),
    .in_2(full_adder_10_out_5));
  full_adder full_adder_13 (
    .out_4(full_adder_6_out_4), .out_5(full_adder_13_out_5), .in_1(and_12_out), .in_3(full_adder_12_out_4),
    .in_2(full_adder_11_out_5));
  and and_13 (and_13_out, in_1[7], in_2[4]);
  full_adder full_adder_14 (
    .out_4(full_adder_14_out_4), .out_5(and_64_out[11]), .in_1(and_13_out), .in_3(full_adder_14_out_4),
    .in_2(full_adder_13_out_5));
  and and_14 (and_14_out, in_1[1], in_2[7]);
  full_adder full_adder_15 (
    .out_4(full_adder_15_out_4), .out_5(full_adder_15_out_5), .in_1(and_14_out), .in_3(full_adder_24_out_4),
    .in_2(1'b0));
  and and_15 (and_15_out, in_1[2], in_2[7]);
  full_adder full_adder_16 (
    .out_4(full_adder_16_out_4), .out_5(full_adder_16_out_5), .in_1(and_26_out), .in_3(full_adder_16_out_4),
    .in_2(full_adder_15_out_5));
  full_adder full_adder_17 (
    .out_4(full_adder_17_out_4), .out_5(full_adder_17_out_5), .in_1(and_15_out), .in_3(full_adder_16_out_4),
    .in_2(full_adder_15_out_4));
  and and_16 (and_16_out, in_1[3], in_2[6]);
  full_adder full_adder_18 (
    .out_4(full_adder_18_out_4), .out_5(full_adder_18_out_5), .in_1(and_16_out), .in_3(full_adder_18_out_4),
    .in_2(full_adder_17_out_5));
  and and_17 (and_17_out, in_1[4], in_2[5]);
  full_adder full_adder_19 (
    .out_4(full_adder_9_out_4), .out_5(full_adder_19_out_5), .in_1(and_17_out), .in_3(full_adder_28_out_4),
    .in_2(full_adder_18_out_5));
  and and_18 (and_18_out, in_1[5], in_2[4]);
  full_adder full_adder_20 (
    .out_4(full_adder_20_out_4), .out_5(full_adder_20_out_5), .in_1(and_18_out), .in_3(full_adder_20_out_4),
    .in_2(full_adder_19_out_5));
  and and_19 (and_19_out, in_1[6], in_2[3]);
  and and_20 (and_20_out, in_1[6], in_2[4]);
  full_adder full_adder_21 (
    .out_4(full_adder_12_out_4), .out_5(full_adder_21_out_5), .in_1(and_19_out), .in_3(full_adder_31_out_4),
    .in_2(full_adder_20_out_5));
  and and_21 (and_21_out, in_1[7], in_2[3]);
  and and_22 (and_22_out, in_1[7], in_2[2]);
  full_adder full_adder_22 (
    .out_4(full_adder_14_out_4), .out_5(and_64_out[10]), .in_1(and_21_out), .in_3(full_adder_23_out_4),
    .in_2(full_adder_12_out_5));
  full_adder full_adder_23 (
    .out_4(full_adder_23_out_4), .out_5(and_64_out[9]), .in_1(and_22_out), .in_3(full_adder_23_out_4),
    .in_2(full_adder_21_out_5));
  and and_23 (and_23_out, in_1[0], in_2[7]);
  and and_24 (and_24_out, in_1[1], in_2[6]);
  full_adder full_adder_24 (
    .out_4(full_adder_24_out_4), .out_5(full_adder_24_out_5), .in_1(and_24_out), .in_3(full_adder_24_out_4),
    .in_2(and_23_out));
  and and_25 (and_25_out, in_1[2], in_2[5]);
  and and_26 (and_26_out, in_1[2], in_2[6]);
  full_adder full_adder_25 (
    .out_4(full_adder_16_out_4), .out_5(full_adder_25_out_5), .in_1(and_25_out), .in_3(full_adder_34_out_4),
    .in_2(full_adder_24_out_5));
  and and_27 (and_27_out, in_1[3], in_2[5]);
  and and_28 (and_28_out, in_1[3], in_2[4]);
  full_adder full_adder_26 (
    .out_4(full_adder_26_out_4), .out_5(full_adder_26_out_5), .in_1(and_28_out), .in_3(full_adder_26_out_4),
    .in_2(full_adder_25_out_5));
  full_adder full_adder_27 (
    .out_4(full_adder_18_out_4), .out_5(full_adder_27_out_5), .in_1(and_27_out), .in_3(full_adder_26_out_4),
    .in_2(full_adder_16_out_5));
  and and_29 (and_29_out, in_1[4], in_2[4]);
  full_adder full_adder_28 (
    .out_4(full_adder_28_out_4), .out_5(full_adder_28_out_5), .in_1(and_39_out), .in_3(full_adder_36_out_4),
    .in_2(full_adder_26_out_5));
  full_adder full_adder_29 (
    .out_4(full_adder_28_out_4), .out_5(full_adder_29_out_5), .in_1(and_29_out), .in_3(full_adder_28_out_4),
    .in_2(full_adder_27_out_5));
  and and_30 (and_30_out, in_1[5], in_2[3]);
  full_adder full_adder_30 (
    .out_4(full_adder_20_out_4), .out_5(full_adder_30_out_5), .in_1(and_30_out), .in_3(full_adder_37_out_4),
    .in_2(full_adder_29_out_5));
  and and_31 (and_31_out, in_1[6], in_2[2]);
  full_adder full_adder_31 (
    .out_4(full_adder_31_out_4), .out_5(full_adder_31_out_5), .in_1(and_31_out), .in_3(full_adder_31_out_4),
    .in_2(full_adder_30_out_5));
  and and_32 (and_32_out, in_1[7], in_2[1]);
  full_adder full_adder_32 (
    .out_4(full_adder_23_out_4), .out_5(and_64_out[8]), .in_1(and_32_out), .in_3(full_adder_41_out_4),
    .in_2(full_adder_31_out_5));
  and and_33 (and_33_out, in_1[0], in_2[6]);
  and and_34 (and_34_out, in_1[0], in_2[5]);
  and and_35 (and_35_out, in_1[1], in_2[5]);
  full_adder full_adder_33 (
    .out_4(full_adder_24_out_4), .out_5(full_adder_33_out_5), .in_1(and_35_out), .in_3(full_adder_42_out_4),
    .in_2(and_33_out));
  and and_36 (and_36_out, in_1[2], in_2[4]);
  full_adder full_adder_34 (
    .out_4(full_adder_34_out_4), .out_5(full_adder_34_out_5), .in_1(and_36_out), .in_3(full_adder_34_out_4),
    .in_2(full_adder_33_out_5));
  and and_37 (and_37_out, in_1[3], in_2[3]);
  full_adder full_adder_35 (
    .out_4(full_adder_26_out_4), .out_5(full_adder_35_out_5), .in_1(and_37_out), .in_3(full_adder_46_out_4),
    .in_2(full_adder_34_out_5));
  and and_38 (and_38_out, in_1[4], in_2[2]);
  and and_39 (and_39_out, in_1[4], in_2[3]);
  full_adder full_adder_36 (
    .out_4(full_adder_36_out_4), .out_5(full_adder_36_out_5), .in_1(and_38_out), .in_3(full_adder_36_out_4),
    .in_2(full_adder_35_out_5));
  and and_40 (and_40_out, in_1[5], in_2[2]);
  and and_41 (and_41_out, in_1[5], in_2[1]);
  full_adder full_adder_37 (
    .out_4(full_adder_37_out_4), .out_5(full_adder_37_out_5), .in_1(and_41_out), .in_3(full_adder_48_out_4),
    .in_2(full_adder_36_out_5));
  full_adder full_adder_38 (
    .out_4(full_adder_37_out_4), .out_5(full_adder_38_out_5), .in_1(and_40_out), .in_3(full_adder_37_out_4),
    .in_2(full_adder_28_out_5));
  and and_42 (and_42_out, in_1[6], in_2[1]);
  full_adder full_adder_39 (
    .out_4(full_adder_39_out_4), .out_5(and_64_out[6]), .in_1(and_51_out), .in_3(full_adder_39_out_4),
    .in_2(full_adder_37_out_5));
  full_adder full_adder_40 (
    .out_4(full_adder_31_out_4), .out_5(full_adder_40_out_5), .in_1(and_42_out), .in_3(full_adder_39_out_4),
    .in_2(full_adder_38_out_5));
  and and_43 (and_43_out, in_1[7], in_2[0]);
  full_adder full_adder_41 (
    .out_4(full_adder_41_out_4), .out_5(and_64_out[7]), .in_1(and_43_out), .in_3(full_adder_41_out_4),
    .in_2(full_adder_40_out_5));
  buf and_44 (and_44_out, in_2[4]);  // AND_Gate
  and and_45 (and_45_out, in_1[1], in_2[3]);
  and and_46 (and_46_out, in_1[1], in_2[4]);
  full_adder full_adder_42 (
    .out_4(full_adder_42_out_4), .out_5(full_adder_42_out_5), .in_1(and_46_out), .in_3(full_adder_42_out_4),
    .in_2(and_34_out));
  full_adder full_adder_43 (
    .out_4(full_adder_42_out_4), .out_5(full_adder_43_out_5), .in_1(and_45_out), .in_3(full_adder_49_out_4),
    .in_2(and_44_out));
  and and_47 (and_47_out, in_1[2], in_2[3]);
  full_adder full_adder_44 (
    .out_4(full_adder_44_out_4), .out_5(full_adder_44_out_5), .in_1(and_55_out), .in_3(full_adder_44_out_4),
    .in_2(full_adder_43_out_5));
  full_adder full_adder_45 (
    .out_4(full_adder_34_out_4), .out_5(full_adder_45_out_5), .in_1(and_47_out), .in_3(full_adder_44_out_4),
    .in_2(full_adder_42_out_5));
  and and_48 (and_48_out, in_1[3], in_2[2]);
  full_adder full_adder_46 (
    .out_4(full_adder_46_out_4), .out_5(full_adder_46_out_5), .in_1(and_48_out), .in_3(full_adder_46_out_4),
    .in_2(full_adder_45_out_5));
  and and_49 (and_49_out, in_1[4], in_2[1]);
  full_adder full_adder_47 (
    .out_4(full_adder_36_out_4), .out_5(full_adder_47_out_5), .in_1(and_49_out), .in_3(full_adder_53_out_4),
    .in_2(full_adder_46_out_5));
  and and_50 (and_50_out, in_1[5], in_2[0]);
  full_adder full_adder_48 (
    .out_4(full_adder_48_out_4), .out_5(and_64_out[5]), .in_1(and_50_out), .in_3(full_adder_48_out_4),
    .in_2(full_adder_47_out_5));
  and and_51 (and_51_out, in_1[6], in_2[0]);
  and and_52 (and_52_out, in_1[0], in_2[3]);
  and and_53 (and_53_out, in_1[1], in_2[2]);
  full_adder full_adder_49 (
    .out_4(full_adder_49_out_4), .out_5(full_adder_49_out_5), .in_1(and_53_out), .in_3(full_adder_49_out_4),
    .in_2(and_52_out));
  and and_54 (and_54_out, in_1[2], in_2[1]);
  and and_55 (and_55_out, in_1[2], in_2[2]);
  full_adder full_adder_50 (
    .out_4(full_adder_44_out_4), .out_5(full_adder_50_out_5), .in_1(and_54_out), .in_3(full_adder_55_out_4),
    .in_2(full_adder_49_out_5));
  and and_56 (and_56_out, in_1[3], in_2[1]);
  and and_57 (and_57_out, in_1[3], in_2[0]);
  full_adder full_adder_51 (
    .out_4(full_adder_51_out_4), .out_5(and_64_out[3]), .in_1(and_57_out), .in_3(full_adder_51_out_4),
    .in_2(full_adder_50_out_5));
  full_adder full_adder_52 (
    .out_4(full_adder_46_out_4), .out_5(full_adder_52_out_5), .in_1(and_56_out), .in_3(full_adder_51_out_4),
    .in_2(full_adder_44_out_5));
  and and_58 (and_58_out, in_1[4], in_2[0]);
  full_adder full_adder_53 (
    .out_4(full_adder_53_out_4), .out_5(and_64_out[4]), .in_1(and_58_out), .in_3(full_adder_53_out_4),
    .in_2(full_adder_52_out_5));
  and and_59 (and_59_out, in_1[0], in_2[2]);
  and and_60 (and_60_out, in_1[0], in_2[1]);
  and and_61 (and_61_out, in_1[1], in_2[1]);
  full_adder full_adder_54 (
    .out_4(full_adder_49_out_4), .out_5(full_adder_54_out_5), .in_1(and_61_out), .in_3(full_adder_56_out_4),
    .in_2(and_59_out));
  and and_62 (and_62_out, in_1[2], in_2[0]);
  full_adder full_adder_55 (
    .out_4(full_adder_55_out_4), .out_5(and_64_out[2]), .in_1(and_62_out), .in_3(full_adder_55_out_4),
    .in_2(full_adder_54_out_5));
  and and_63 (and_63_out, in_1[1], in_2[0]);
  full_adder full_adder_56 (
    .out_4(full_adder_56_out_4), .out_5(and_64_out[1]), .in_1(and_63_out), .in_3(full_adder_56_out_4),
    .in_2(and_60_out));
  and and_64 (and_64_out[0], in_1[0], in_2[0]);
  assign out_4 = in_3 ? and_64_out : 16'bz;  // Controlled_Buffer controlled_buffer_1
  // also tied to GND on the sheet: {full_adder_41_out_4, full_adder_48_out_4, full_adder_53_out_4, full_adder_39_out_4, full_adder_51_out_4, full_adder_55_out_4, full_adder_56_out_4}
endmodule

module ALU_4bit (
  input  [3:0] in_1,
  input  [3:0] in_2,
  input  [3:0] in_3,
  input  in_4,
  input  Cn,
  input  M,
  output G,
  output Cn_4,
  output P,
  output [3:0] out_10
);

  wire and_1_out, and_2_out, and_3_out, and_4_out, and_5_out, and_6_out, and_7_out, and_8_out, and_9_out,
       and_10_out, and_11_out, and_12_out, and_13_out, and_14_out, and_15_out, and_16_out, and_17_out,
       and_18_out, and_19_out, and_20_out, and_21_out, and_22_out, and_23_out, and_24_out, and_25_out,
       and_26_out, and_27_out, and_28_out, and_29_out, and_30_out, and_31_out, and_32_out, and_33_out,
       and_34_out, and_35_out, and_36_out, and_37_out, and_38_out, full_adder_2_out_4, full_adder_3_out_4,
       full_adder_4_out_4, nand_1_out, nand_3_out, nor_1_out, nor_2_out, nor_3_out, nor_4_out, nor_5_out,
       nor_6_out, nor_7_out, nor_8_out, nor_10_out, nor_11_out, nor_12_out, not_1_out, not_2_out, not_3_out,
       not_4_out, not_5_out, not_6_out, not_7_out, not_8_out, not_9_out, not_10_out, not_11_out, xor_1_out,
       xor_2_out, xor_3_out, xor_4_out, xor_5_out;

  not not_1 (not_1_out, in_2[3]);
  not not_2 (not_2_out, in_2[2]);
  not not_3 (not_3_out, in_2[1]);
  not not_4 (not_4_out, in_2[0]);
  not not_5 (not_5_out, M);
  and and_1 (and_1_out, in_2[3], in_1[3], in_3[3]);
  and and_2 (and_2_out, in_3[3], in_1[2], not_1_out);
  and and_3 (and_3_out, not_1_out, in_1[1]);
  and and_4 (and_4_out, in_1[0], in_2[3]);
  and and_5 (and_5_out, in_3[3], in_3[3]);
  and and_6 (and_6_out, in_2[2], in_1[3], in_3[2]);
  and and_7 (and_7_out, in_3[2], in_1[2], not_2_out);
  and and_8 (and_8_out, not_2_out, in_1[1]);
  and and_9 (and_9_out, in_1[0], in_2[2]);
  and and_10 (and_10_out, in_3[2], in_3[2]);
  and and_11 (and_11_out, in_1[3], in_2[1], in_3[1]);
  and and_12 (and_12_out, in_3[1], in_1[2], not_3_out);
  and and_13 (and_13_out, not_3_out, in_1[1]);
  and and_14 (and_14_out, in_1[0], in_2[1]);
  and and_15 (and_15_out, in_3[1], in_3[1]);
  and and_16 (and_16_out, in_1[3], in_2[0], in_3[0]);
  and and_17 (and_17_out, in_3[0], in_1[2], not_4_out);
  and and_18 (and_18_out, in_1[1], not_4_out);
  and and_19 (and_19_out, in_1[0], in_2[0]);
  and and_20 (and_20_out, in_3[0], in_3[0]);
  nor nor_1 (nor_1_out, and_1_out, and_2_out);
  nor nor_2 (nor_2_out, and_3_out, and_4_out, and_5_out);
  nor nor_3 (nor_3_out, and_6_out, and_7_out);
  nor nor_4 (nor_4_out, and_8_out, and_9_out, and_10_out);
  nor nor_5 (nor_5_out, and_11_out, and_12_out);
  nor nor_6 (nor_6_out, and_13_out, and_14_out, and_15_out);
  nor nor_7 (nor_7_out, and_16_out, and_17_out);
  nor nor_8 (nor_8_out, and_18_out, and_19_out, and_20_out);
  and and_21 (and_21_out, nor_2_out, nor_2_out);
  and and_22 (and_22_out, nor_1_out, nor_4_out);
  and and_23 (and_23_out, nor_1_out, nor_3_out, nor_6_out);
  and and_24 (and_24_out, nor_1_out, nor_5_out, nor_6_out, nor_8_out);
  nand nand_1 (nand_1_out, nor_1_out, nor_3_out, nor_5_out, nor_7_out, Cn);
  nand nand_2 (P, nor_1_out, nor_3_out, nor_5_out, nor_7_out);
  not not_6 (not_6_out, nor_2_out);
  and and_25 (and_25_out, nor_3_out, nor_5_out, nor_7_out, Cn, not_5_out);
  and and_26 (and_26_out, nor_3_out, nor_5_out, nor_8_out, not_5_out);
  and and_27 (and_27_out, nor_3_out, nor_6_out, not_5_out);
  and and_28 (and_28_out, nor_4_out, not_5_out);
  not not_7 (not_7_out, nor_4_out);
  and and_29 (and_29_out, nor_5_out, nor_7_out, Cn, not_5_out);
  and and_30 (and_30_out, nor_5_out, nor_8_out, not_5_out);
  and and_31 (and_31_out, nor_6_out, not_5_out);
  not not_8 (not_8_out, nor_6_out);
  and and_32 (and_32_out, Cn, nor_7_out, not_5_out);
  and and_33 (and_33_out, nor_8_out, not_5_out);
  not not_9 (not_9_out, nor_8_out);
  nor nor_9 (G, and_21_out, and_22_out, and_23_out, and_24_out);
  not not_10 (not_10_out, nand_1_out);
  and and_34 (and_34_out, nor_1_out, not_6_out);
  and and_35 (and_35_out, nor_3_out, not_7_out);
  nor nor_10 (nor_10_out, and_29_out, and_30_out, and_31_out);
  and and_36 (and_36_out, nor_5_out, not_8_out);
  nor nor_11 (nor_11_out, and_32_out, and_33_out);
  and and_37 (and_37_out, nor_7_out, not_9_out);
  nand nand_3 (nand_3_out, not_5_out, Cn);
  or or_1 (Cn_4, not_10_out, not_11_out);
  not not_11 (not_11_out, G);
  nor nor_12 (nor_12_out, and_25_out, and_26_out, and_27_out, and_28_out);
  xor xor_1 (xor_1_out, and_34_out, nor_12_out);
  xor xor_2 (xor_2_out, and_35_out, nor_10_out);
  and and_38 (and_38_out, xor_1_out, xor_2_out, xor_3_out, xor_4_out);
  xor xor_3 (xor_3_out, and_36_out, nor_11_out);
  xor xor_4 (xor_4_out, and_37_out, nand_3_out);
  xor xor_5 (xor_5_out, xor_4_out, 1'b0);
  full_adder full_adder_1 (.out_5(out_10[3]), .in_1(1'b0), .in_3(full_adder_2_out_4), .in_2(xor_1_out));  // open: out_4
  full_adder full_adder_2 (
    .out_4(full_adder_2_out_4), .out_5(out_10[2]), .in_1(1'b0), .in_3(full_adder_3_out_4), .in_2(xor_2_out));
  full_adder full_adder_3 (
    .out_4(full_adder_3_out_4), .out_5(out_10[1]), .in_1(1'b0), .in_3(full_adder_4_out_4), .in_2(xor_3_out));
  full_adder full_adder_4 (.out_4(full_adder_4_out_4), .out_5(out_10[0]), .in_1(1'b0), .in_3(in_4), .in_2(xor_5_out));
endmodule

module coder_circuit (
  input  [6:0] in_1,
  output [2:0] out_2
);

  wire and_1_out, and_2_out, and_3_out, nand_1_out, not_1_out, not_2_out, not_3_out, not_4_out, not_5_out,
       not_6_out, not_7_out, not_8_out;

  not not_1 (not_1_out, in_1[0]);
  not not_2 (not_2_out, in_1[2]);
  not not_3 (not_3_out, in_1[4]);
  not not_4 (not_4_out, in_1[6]);
  not not_5 (not_5_out, in_1[1]);
  not not_6 (not_6_out, in_1[5]);
  not not_7 (not_7_out, in_1[5]);
  not not_8 (not_8_out, in_1[3]);
  nand nand_1 (nand_1_out, not_8_out, not_2_out, not_5_out, not_4_out, not_1_out, not_3_out, not_7_out);
  and and_1 (and_1_out, not_2_out, not_1_out, not_4_out, not_3_out, nand_1_out);
  and and_2 (and_2_out, not_5_out, not_1_out, in_1[6], nand_1_out, not_3_out, not_6_out);
  and and_3 (and_3_out, nand_1_out, not_1_out, not_5_out, not_2_out, not_8_out, in_1[6]);
  or or_1 (out_2[0], and_1_out, in_1[1], in_1[3], in_1[5]);
  or or_2 (out_2[1], and_2_out, in_1[3], in_1[2]);
  or or_3 (out_2[2], and_3_out, in_1[5], in_1[4]);
endmodule

module Bi_comparator (
  input  [3:0] in_1,
  input  [3:0] in_2,
  input  in_3,
  input  in_4,
  input  in_5,
  output out_6,
  output out_7,
  output out_8
);

  wire and_1_out, and_2_out, and_3_out, and_4_out, and_5_out, and_6_out, and_7_out, and_8_out, and_9_out,
       and_10_out, and_11_out, and_12_out, and_13_out, and_14_out, and_15_out, and_17_out, and_18_out,
       and_19_out, and_20_out, and_21_out, nand_1_out, nand_2_out, nand_3_out, nand_4_out, nor_1_out,
       nor_2_out, nor_3_out, nor_4_out;

  and and_1 (and_1_out, in_1[3], nand_1_out);
  nand nand_1 (nand_1_out, in_2[3], in_1[3]);
  and and_2 (and_2_out, nand_1_out, in_2[3]);
  nand nand_2 (nand_2_out, in_1[2], in_2[2]);
  nand nand_3 (nand_3_out, in_1[1], in_2[1]);
  nand nand_4 (nand_4_out, in_1[0], in_2[0]);
  nor nor_1 (nor_1_out, and_1_out, and_2_out);
  and and_3 (and_3_out, in_1[2], nand_2_out);
  nor nor_2 (nor_2_out, and_3_out, and_4_out);
  and and_4 (and_4_out, nand_2_out, in_2[2]);
  and and_5 (and_5_out, in_1[1], nand_3_out);
  nor nor_3 (nor_3_out, and_5_out, and_6_out);
  and and_6 (and_6_out, nand_3_out, in_2[1]);
  and and_7 (and_7_out, in_1[0], nand_4_out);
  and and_8 (and_8_out, nand_4_out, in_2[0]);
  and and_9 (and_9_out, nand_1_out, in_1[3]);
  and and_10 (and_10_out, nand_1_out, in_2[3]);
  nor nor_4 (nor_4_out, and_7_out, and_8_out);
  and and_11 (and_11_out, nor_1_out, in_2[2], nand_2_out);
  and and_12 (and_12_out, in_2[1], nand_3_out, nor_1_out, nor_2_out);
  and and_13 (and_13_out, nor_1_out, in_2[0], nand_4_out, nor_3_out, nor_2_out);
  and and_14 (and_14_out, nor_1_out, nor_2_out, nor_3_out, nor_4_out, in_3);
  and and_15 (and_15_out, nor_1_out, nor_2_out, nor_3_out, nor_4_out, in_4);
  and and_16 (out_7, nor_1_out, nor_2_out, in_4, nor_3_out, nor_4_out);
  and and_17 (and_17_out, in_4, nor_4_out, nor_3_out, nor_2_out, nor_1_out);
  and and_18 (and_18_out, nor_3_out, nor_4_out, nor_2_out, in_5, nor_1_out);
  and and_19 (and_19_out, in_1[0], nand_4_out, nor_3_out, nor_2_out, nor_1_out);
  and and_20 (and_20_out, in_1[1], nand_3_out, nor_2_out, nor_1_out);
  and and_21 (and_21_out, nor_1_out, nand_2_out, in_1[2]);
  nor nor_5 (out_6, and_10_out, and_11_out, and_12_out, and_13_out, and_14_out, and_15_out);
  nor nor_6 (out_8, and_17_out, and_18_out, and_19_out, and_20_out, and_21_out, and_9_out);
endmodule

module ALU_1bit_Arthi (
  input  [2:0] in_1,
  input  in_2,
  input  in_3,
  input  in_4,
  input  in_5,
  input  [2:0] in_6,
  output out_7,
  output out_8,
  output out_9
);

  wire and_1_out, and_2_out, and_3_out, and_4_out, nor_1_out, or_1_out, or_2_out, xor_1_out, xor_2_out;

  xor xor_1 (xor_1_out, in_3, in_4);
  and and_1 (and_1_out, in_6[2], in_2);
  and and_2 (and_2_out, 1'b0, in_6[1]);
  and and_3 (and_3_out, in_2, in_3);
  or or_1 (or_1_out, in_2, in_3);
  xor xor_2 (xor_2_out, in_2, in_3);
  nor nor_1 (nor_1_out, in_2, in_3);
  full_adder full_adder_1 (.out_4(out_8), .out_5(out_9), .in_1(in_2), .in_3(in_5), .in_2(xor_1_out));
  and and_4 (and_4_out, in_3, in_6[0]);
  or or_2 (or_2_out, and_4_out, and_1_out, and_2_out);
  Multiplexer #(.select(3)) multiplexer_1 (
    .in0(and_3_out), .in1(or_1_out), .in2(xor_2_out), .in3(nor_1_out), .in4(out_9), .in5(out_9),
    .in6(or_2_out), .out(out_7), .sel(in_1));  // open: in7, en
endmodule

module _2s_complement (
  input  [3:0] in_1,
  input  in_2,
  input  in_3,
  output [3:0] out_4,
  output out_5
);

  wire full_adder_1_out_4, full_adder_2_out_4, full_adder_3_out_4, not_1_out, not_2_out, not_3_out, not_4_out;
  wire [3:0] full_adder_1_out_5;

  not not_1 (not_1_out, in_1[0]);
  not not_2 (not_2_out, in_1[1]);
  not not_3 (not_3_out, in_1[2]);
  not not_4 (not_4_out, in_1[3]);
  full_adder full_adder_1 (
    .out_4(full_adder_1_out_4), .out_5(full_adder_1_out_5[0]), .in_1(not_1_out), .in_3(in_3), .in_2(1'b0));
  full_adder full_adder_2 (
    .out_4(full_adder_2_out_4), .out_5(full_adder_1_out_5[1]), .in_1(not_2_out), .in_3(full_adder_1_out_4),
    .in_2(1'b0));
  full_adder full_adder_3 (
    .out_4(full_adder_3_out_4), .out_5(full_adder_1_out_5[2]), .in_1(not_3_out), .in_3(full_adder_2_out_4),
    .in_2(1'b0));
  full_adder full_adder_4 (
    .out_4(out_5), .out_5(full_adder_1_out_5[3]), .in_1(not_4_out), .in_3(full_adder_3_out_4), .in_2(1'b0));
  assign out_4 = in_2 ? full_adder_1_out_5 : 4'bz;  // Controlled_Buffer controlled_buffer_1
endmodule

module Number_display (
  input  in_1,
  input  [7:0] in_2,
  output [31:0] out_3
);

  wire [15:0] rom_1_data;
  wire [31:0] rom_5_data;

  ROM #(.dataWidth(16)) rom_1 (.addr(in_2), .data(rom_1_data));  // open: sel
  ROM #(.addrWidth(4)) rom_2 (.addr(rom_1_data[3:0]), .data(rom_5_data[31:24]));  // open: sel
  ROM #(.addrWidth(4)) rom_3 (.addr(rom_1_data[7:4]), .data(rom_5_data[23:16]));  // open: sel
  ROM #(.addrWidth(4)) rom_4 (.addr(rom_1_data[11:8]), .data(rom_5_data[15:8]));  // open: sel
  ROM #(.addrWidth(4)) rom_5 (.addr(rom_1_data[15:12]), .data(rom_5_data[7:0]));  // open: sel
  assign out_3 = in_1 ? rom_5_data : 32'bz;  // Controlled_Buffer controlled_buffer_1

  // Notes on the sheet:
  //   contents of rom_1 (hex, n*v repeats v):
  //   0 1 2 3 4 5 6 7 8 9 10 11 12 13 14 15 16 17 18 19 20 21 22 23 24 25 26 27 28 29 30 31 32 33 34 35 36
  //   37 38 39 40 41 42 43 44 45 46 47 48 49 50 51 52 53 54 55 56 57 58 59 60 61 62 63 64 65 66 67 68 69
  //   70 71 72 73 74 75 76 77 78 79 80 81 82 83 84 85 86 87 88 89 90 91 92 93 94 95 96 97 98 99 100 101
  //   102 103 104 105 106 107 108 109 110 111 112 113 114 115 116 117 118 119 120 121 122 123 124 125 126
  //   127 128 129 130 131 132 133 134 135 136 137 138 139 140 141 142 143 144 145 146 147 148 149 150 151
  //   152 153 154 155 156 157 158 159 160 161 162 163 164 165 166 167 168 169 170 171 172 173 174 175 176
  //   177 178 179 180 181 182 183 184 185 186 187 188 189 190 191 192 193 194 195 196 197 198 199 200 201
  //   202 203 204 205 206 207 208 209 210 211 212 213 214 215 216 217 218 219 220 221 222 223 224 225 226
  //   227 228 229 230 231 232 233 234 235 236 237 238 239 240 241 242 243 244 245 246 247 248 249 250 251
  //   252 253 254 255
  //   contents of rom_2 (hex, n*v repeats v):
  //   7e 48 3d 6d 4b 67 77 4c 7f 6f 7e 48 3d 6d 4b 67
  //   contents of rom_3 (hex, n*v repeats v):
  //   7e 48 3d 6d 4b 67 77 4c 7f 6f 7e 48 3d 6d 4b 67
  //   contents of rom_4 (hex, n*v repeats v):
  //   7e 48 3d 6d 4b 67 77 4c 7f 6f 7e 48 3d 6d 4b 67
  //   contents of rom_5 (hex, n*v repeats v):
  //   7e 48 3d 6d 4b 67 77 4c 7f 6f 7e 48 3d 6d 4b 67
endmodule
